// Digital circuit ALU.dig as structural Verilog
module ALU (
  input  [15:0] Left_Hand_Bus,
  input  [15:0] Right_Hand_Bus,
  input  Carry_In,
  input  [4:0] Instruction,
  input  EO,
  input  CLKEdge,
  input  EIN,
  input  BRO,
  output [15:0] Result,
  output Carry_Out,
  output Signed,
  output Overflow,
  output Zero
);

  wire _74283_1_pin9, _74283_2_pin9, _74283_3_pin9, _74283_4_pin9, and_2_out, and_3_out, and_4_out,
       and_5_out, and_6_out, and_7_out, and_8_out, and_9_out, and_10_out, and_11_out, and_12_out, and_13_out,
       and_14_out, and_15_out, and_16_out, and_18_out, and_19_out, and_20_out, Arithmetic, Bitwise,
       BitwiseMode1, BitwiseMode2, CarryIn, Logical, LogicalShift, Not, not_1_out, not_2_out, not_3_out,
       not_6_out, not_7_out, or_4_out, Shift, xor_3_out, xor_5_out, xor_6_out;
  wire [0:0] or_2_out;
  wire [14:0] driver_8_out;
  wire [15:0] _74283_2_pin4, and_1_out, driver_1_out, LogicalResult, or_1_out, xor_1_out, xor_2_out,
       xor_4_out;
  wire [15:15] or_3_out;

  assign and_1_out = Left_Hand_Bus & Right_Hand_Bus;  // And and_1, 16 bits wide
  assign or_1_out = Left_Hand_Bus | Right_Hand_Bus;  // Or or_1, 16 bits wide
  assign xor_1_out = Left_Hand_Bus ^ Right_Hand_Bus;  // XOr xor_1, 16 bits wide
  assign driver_1_out = and_3_out ? Right_Hand_Bus : 16'bz;  // Driver driver_1
  assign driver_1_out = and_4_out ? and_1_out : 16'bz;  // Driver driver_2
  assign driver_1_out = and_5_out ? or_1_out : 16'bz;  // Driver driver_3
  assign driver_1_out = and_6_out ? xor_1_out : 16'bz;  // Driver driver_4
  and and_2 (and_2_out, CLKEdge, EIN);
  assign xor_2_out = driver_1_out ^ {16{Not}};  // XOr xor_2, 16 bits wide
  assign LogicalResult = Bitwise ? xor_2_out : 16'bz;  // Driver driver_5
  and and_3 (and_3_out, not_2_out, not_1_out);
  and and_4 (and_4_out, BitwiseMode1, not_2_out);
  and and_5 (and_5_out, BitwiseMode2, not_1_out);
  and and_6 (and_6_out, BitwiseMode2, BitwiseMode1);
  not not_1 (not_1_out, BitwiseMode1);
  not not_2 (not_2_out, BitwiseMode2);
  and and_7 (and_7_out, not_3_out, and_2_out);
  not not_3 (not_3_out, Instruction[4]);
  and and_8 (and_8_out, and_2_out, Instruction[4]);
  nor nor_1 (Logical, and_7_out, Arithmetic);
  nor nor_2 (Arithmetic, Logical, and_8_out);
  _74173 _74173_1 (
    .pin1(1'b0), .pin2(1'b0), .pin3(Bitwise), .pin4(Not), .pin5(BitwiseMode2), .pin6(BitwiseMode1),
    .pin7(and_2_out), .pin8(1'b0), .pin9(1'b0), .pin10(1'b0), .pin11(Instruction[0]), .pin12(Instruction[1]),
    .pin13(Instruction[2]), .pin14(Instruction[3]), .pin15(1'b0), .pin16(1'b1));
  not not_4 (LogicalShift, Not);
  not not_5 (Shift, Bitwise);
  and and_9 (and_9_out, LogicalShift, CarryIn);
  and and_10 (and_10_out, Right_Hand_Bus[15], Not);
  and and_11 (and_11_out, BitwiseMode2, Shift);
  and and_12 (and_12_out, Right_Hand_Bus[0], Not);
  or or_2 (or_2_out[0], and_10_out, and_9_out);
  and and_13 (and_13_out, Right_Hand_Bus[15], and_11_out);
  and and_14 (and_14_out, not_6_out, Shift);
  not not_6 (not_6_out, BitwiseMode2);
  and and_15 (and_15_out, and_14_out, Right_Hand_Bus[0]);
  or or_3 (or_3_out[15], and_12_out, and_9_out);
  or or_4 (or_4_out, and_13_out, and_15_out);
  assign LogicalResult = and_11_out ? {Right_Hand_Bus[14:0], or_2_out[0]} : 16'bz;  // Driver driver_6
  and and_16 (and_16_out, or_4_out, LogicalShift);
  assign LogicalResult = and_14_out ? {or_3_out[15], Right_Hand_Bus[15:1]} : 16'bz;  // Driver driver_7
  and and_17 (CarryIn, Carry_In, BitwiseMode1);
  xor xor_3 (xor_3_out, CarryIn, BitwiseMode2);
  assign xor_4_out = Right_Hand_Bus ^ {16{BitwiseMode2}};  // XOr xor_4, 16 bits wide
  _74283 _74283_1 (
    .pin1(_74283_2_pin4[1]), .pin2(xor_4_out[1]), .pin3(Left_Hand_Bus[1]), .pin4(_74283_2_pin4[0]),
    .pin5(Left_Hand_Bus[0]), .pin6(xor_4_out[0]), .pin7(xor_3_out), .pin8(1'b0), .pin9(_74283_1_pin9),
    .pin10(_74283_2_pin4[3]), .pin11(xor_4_out[3]), .pin12(Left_Hand_Bus[3]), .pin13(_74283_2_pin4[2]),
    .pin14(Left_Hand_Bus[2]), .pin15(xor_4_out[2]), .pin16(1'b1));
  _74283 _74283_2 (
    .pin1(_74283_2_pin4[5]), .pin2(xor_4_out[5]), .pin3(Left_Hand_Bus[5]), .pin4(_74283_2_pin4[4]),
    .pin5(Left_Hand_Bus[4]), .pin6(xor_4_out[4]), .pin7(_74283_1_pin9), .pin8(1'b0), .pin9(_74283_2_pin9),
    .pin10(_74283_2_pin4[7]), .pin11(xor_4_out[7]), .pin12(Left_Hand_Bus[7]), .pin13(_74283_2_pin4[6]),
    .pin14(Left_Hand_Bus[6]), .pin15(xor_4_out[6]), .pin16(1'b1));
  _74283 _74283_3 (
    .pin1(_74283_2_pin4[9]), .pin2(xor_4_out[9]), .pin3(Left_Hand_Bus[9]), .pin4(_74283_2_pin4[8]),
    .pin5(Left_Hand_Bus[8]), .pin6(xor_4_out[8]), .pin7(_74283_2_pin9), .pin8(1'b0), .pin9(_74283_3_pin9),
    .pin10(_74283_2_pin4[11]), .pin11(xor_4_out[11]), .pin12(Left_Hand_Bus[11]), .pin13(_74283_2_pin4[10]),
    .pin14(Left_Hand_Bus[10]), .pin15(xor_4_out[10]), .pin16(1'b1));
  _74283 _74283_4 (
    .pin1(_74283_2_pin4[13]), .pin2(xor_4_out[13]), .pin3(Left_Hand_Bus[13]), .pin4(_74283_2_pin4[12]),
    .pin5(Left_Hand_Bus[12]), .pin6(xor_4_out[12]), .pin7(_74283_3_pin9), .pin8(1'b0), .pin9(_74283_4_pin9),
    .pin10(_74283_2_pin4[15]), .pin11(xor_4_out[15]), .pin12(Left_Hand_Bus[15]), .pin13(_74283_2_pin4[14]),
    .pin14(Left_Hand_Bus[14]), .pin15(xor_4_out[14]), .pin16(1'b1));
  and and_18 (and_18_out, _74283_4_pin9, Arithmetic);
  or or_5 (Carry_Out, and_18_out, and_16_out);
  assign {Signed, driver_8_out} = Arithmetic ? _74283_2_pin4 : 16'bz;  // Driver driver_8
  not not_7 (not_7_out, BRO);
  assign {Signed, driver_8_out} = Logical ? LogicalResult : 16'bz;  // Driver driver_9
  and and_19 (and_19_out, not_7_out, EO);
  assign Result = and_19_out ? {Signed, driver_8_out} : 16'bz;  // Driver driver_10
  assign Result = BRO ? Right_Hand_Bus : 16'bz;  // Driver driver_11
  nor nor_3 (Zero, driver_8_out[7], driver_8_out[6], driver_8_out[5], driver_8_out[4], driver_8_out[3], driver_8_out[2], driver_8_out[1], driver_8_out[0], driver_8_out[8], driver_8_out[9], driver_8_out[10], driver_8_out[11], driver_8_out[12], driver_8_out[13], driver_8_out[14], Signed);
  xor xor_5 (xor_5_out, Left_Hand_Bus[15], Signed);
  xor xor_6 (xor_6_out, Signed, Right_Hand_Bus[15]);
  and and_20 (and_20_out, xor_5_out, xor_6_out);
  and and_21 (Overflow, and_20_out, Arithmetic);

  // Other names for the same wires on the sheet: LHBus[15:0] = Left_Hand_Bus; LHSign = Left_Hand_Bus[15];
  //   RHBus[15:0] = Right_Hand_Bus; RHSign = Right_Hand_Bus[15]; Rotate = Not; Direction = BitwiseMode2;
  //   Subtract = BitwiseMode2; UseCarry = BitwiseMode1

  // Notes on the sheet:
  //   Left_Hand_Bus: Left hand input of operation.
  //   Ignored for logical shift operations
  //   Right_Hand_Bus: Right hand input of operations.
  //   Used for logical shift operations
  //   Result: Result of the operation
  //   Carry_Out: Carry flag from the most recent operation.
  //   Carry flag is set from the following operations:
  //   Add
  //   Subract
  //   Shift
  //   Signed: Flag if the result is signed. Set by all operations
  //   (Might want to take off the and/or/etc from setting this
  //   Zero: Zero flag. Set by all operations if the result is Zero
  //   Instruction: Bit 5 will say arithmetic if off, logical if on
  //   If Bit 5 off (Arithmetic Mode) - 0XXSC
  //   	Bit 4 & 3 ignored
  //   	Bit 2 Subtract mode if on
  //   	Bit 1 Uses carry
  //   If Bit 5 on (logic mode)
  //   	If Bit 4 off (bitwise mode) - 10NMM
  //   		Bit 3 Nots result
  //   		Bits 2 & 1 determine function to use
  //   			00 - Unchanged
  //   			01 - And
  //   			10 - Or
  //   			11 - Xor
  //   	If Bit 4 on (shift mode) - 11RDC
  //   		Bit 3 does logical shift if off, rotate if on
  //   		Bit 2 does Direction (right off, left on)
  //   		Bit 1 does Use Carry (ignored for rot)
  //   EO: ALU Result Out
  //   CLKEdge: Rising edge of clock
  //   EIN: ALU Instruction register in
  //   BRO: Bypass Right Hand Bus Out
  //   This is used for the Register Controller
  //   to output a register on the RHBus to the
  //   main bus
  //   Bitwise Logic
  //   Instructions
  //   Bit 5 D Latch
  //   Or just use another 173
  //   Shifting
  //   Inputs
  //   Adder
  //   Results
endmodule
