// Digital circuit RegisterController.dig as structural Verilog
module RegisterController (
  input  Crement,
  input  RCIi,
  input  [15:0] Bus,
  input  CLK,
  input  Reset,
  input  SI1,
  input  SI2,
  input  SPR,
  input  SI3,
  input  SIO1,
  input  SIO2,
  input  SIO3,
  output R1i,
  output R2i,
  output R3i,
  output R4i,
  output R5i,
  output R6i,
  output R7i,
  output R8i,
  output R9i,
  output R10i,
  output R11i,
  output R12i,
  output R13i,
  output R14i,
  output R15i,
  output R0i,
  output LHO1i,
  output LHO2i,
  output LHO3i,
  output LHO4i,
  output LHO5i,
  output LHO6i,
  output LHO7i,
  output LHO8i,
  output LHO9i,
  output LHO10i,
  output LHO11i,
  output LHO12i,
  output LHO13i,
  output LHO14i,
  output LHO15i,
  output LHO0i,
  output RHO1i,
  output RHO2i,
  output RHO3i,
  output RHO4i,
  output RHO5i,
  output RHO6i,
  output RHO7i,
  output RHO8i,
  output RHO9i,
  output RHO10i,
  output RHO11i,
  output RHO12i,
  output RHO13i,
  output RHO14i,
  output RHO15i,
  output RHO0i,
  output Decrement,
  output Increment,
  output SE1,
  output SE2,
  output SE3,
  output SE4,
  output SE5,
  output SE6,
  output SE7,
  output SE8,
  output SOE1,
  output SOE2,
  output SOE3,
  output SOE4,
  output SOE5,
  output SOE6,
  output SOE7,
  output SOE8
);

  wire _74173_1_pin3, _74173_1_pin4, _74173_1_pin5, _74173_1_pin6, _74173_2_pin3, _74173_2_pin4,
       _74173_2_pin5, _74173_2_pin6, _74173_3_pin3, _74173_3_pin4, _74173_3_pin5, _74173_3_pin6, not_1_out;

  _74173 _74173_1 (
    .pin1(1'b0), .pin2(1'b0), .pin3(_74173_1_pin3), .pin4(_74173_1_pin4), .pin5(_74173_1_pin5),
    .pin6(_74173_1_pin6), .pin7(CLK), .pin8(1'b0), .pin9(RCIi), .pin10(RCIi), .pin11(Bus[8]), .pin12(Bus[9]),
    .pin13(Bus[10]), .pin14(Bus[11]), .pin15(Reset), .pin16(1'b1));
  _74138 _74138_1 (
    .pin1(_74173_1_pin6), .pin2(_74173_1_pin5), .pin3(_74173_1_pin4), .pin4(SPR), .pin5(_74173_1_pin3),
    .pin6(1'b1), .pin7(LHO7i), .pin8(1'b0), .pin9(LHO6i), .pin10(LHO5i), .pin11(LHO4i), .pin12(LHO3i),
    .pin13(LHO2i), .pin14(LHO1i), .pin15(LHO0i), .pin16(1'b1));
  _74138 _74138_2 (
    .pin1(_74173_1_pin6), .pin2(_74173_1_pin5), .pin3(_74173_1_pin4), .pin4(SPR), .pin5(SPR),
    .pin6(_74173_1_pin3), .pin7(LHO15i), .pin8(1'b0), .pin9(LHO14i), .pin10(LHO13i), .pin11(LHO12i),
    .pin12(LHO11i), .pin13(LHO10i), .pin14(LHO9i), .pin15(LHO8i), .pin16(1'b1));
  _74173 _74173_2 (
    .pin1(1'b0), .pin2(1'b0), .pin3(_74173_2_pin3), .pin4(_74173_2_pin4), .pin5(_74173_2_pin5),
    .pin6(_74173_2_pin6), .pin7(CLK), .pin8(1'b0), .pin9(RCIi), .pin10(RCIi), .pin11(Bus[4]), .pin12(Bus[5]),
    .pin13(Bus[6]), .pin14(Bus[7]), .pin15(Reset), .pin16(1'b1));
  _74138 _74138_3 (
    .pin1(_74173_2_pin6), .pin2(_74173_2_pin5), .pin3(_74173_2_pin4), .pin4(SPR), .pin5(_74173_2_pin3),
    .pin6(1'b1), .pin7(RHO7i), .pin8(1'b0), .pin9(RHO6i), .pin10(RHO5i), .pin11(RHO4i), .pin12(RHO3i),
    .pin13(RHO2i), .pin14(RHO1i), .pin15(RHO0i), .pin16(1'b1));
  _74138 _74138_4 (
    .pin1(_74173_2_pin6), .pin2(_74173_2_pin5), .pin3(_74173_2_pin4), .pin4(SPR), .pin5(SPR),
    .pin6(_74173_2_pin3), .pin7(RHO15i), .pin8(1'b0), .pin9(RHO14i), .pin10(RHO13i), .pin11(RHO12i),
    .pin12(RHO11i), .pin13(RHO10i), .pin14(RHO9i), .pin15(RHO8i), .pin16(1'b1));
  and and_1 (Decrement, not_1_out, Crement);
  not not_1 (not_1_out, _74173_2_pin6);
  and and_2 (Increment, Crement, _74173_2_pin6);
  _74173 _74173_3 (
    .pin1(1'b0), .pin2(1'b0), .pin3(_74173_3_pin3), .pin4(_74173_3_pin4), .pin5(_74173_3_pin5),
    .pin6(_74173_3_pin6), .pin7(CLK), .pin8(1'b0), .pin9(RCIi), .pin10(RCIi), .pin11(Bus[0]), .pin12(Bus[1]),
    .pin13(Bus[2]), .pin14(Bus[3]), .pin15(Reset), .pin16(1'b1));
  _74138 _74138_5 (
    .pin1(_74173_3_pin6), .pin2(_74173_3_pin5), .pin3(_74173_3_pin4), .pin4(SPR), .pin5(_74173_3_pin3),
    .pin6(1'b1), .pin7(R7i), .pin8(1'b0), .pin9(R6i), .pin10(R5i), .pin11(R4i), .pin12(R3i), .pin13(R2i),
    .pin14(R1i), .pin15(R0i), .pin16(1'b1));
  _74138 _74138_6 (
    .pin1(_74173_3_pin6), .pin2(_74173_3_pin5), .pin3(_74173_3_pin4), .pin4(SPR), .pin5(SPR),
    .pin6(_74173_3_pin3), .pin7(R15i), .pin8(1'b0), .pin9(R14i), .pin10(R13i), .pin11(R12i), .pin12(R11i),
    .pin13(R10i), .pin14(R9i), .pin15(R8i), .pin16(1'b1));
  _74138 _74138_7 (
    .pin1(SI1), .pin2(SI2), .pin3(SI3), .pin4(1'b0), .pin5(1'b0), .pin6(SPR), .pin7(SE8), .pin8(1'b0),
    .pin9(SE7), .pin10(SE6), .pin11(SE5), .pin12(SE4), .pin13(SE3), .pin14(SE2), .pin15(SE1), .pin16(1'b1));
  _74138 _74138_8 (
    .pin1(SIO1), .pin2(SIO2), .pin3(SIO3), .pin4(1'b0), .pin5(1'b0), .pin6(SPR), .pin7(SOE8), .pin8(1'b0),
    .pin9(SOE7), .pin10(SOE6), .pin11(SOE5), .pin12(SOE4), .pin13(SOE3), .pin14(SOE2), .pin15(SOE1),
    .pin16(1'b1));

  // Notes on the sheet:
  //   R1i: Enable for Register 1
  //   R2i: Enable for Register 1
  //   R3i: Enable for Register 1
  //   R4i: Enable for Register 1
  //   R5i: Enable for Register 1
  //   R6i: Enable for Register 1
  //   R7i: Enable for Register 1
  //   R8i: Enable for Register 1
  //   R9i: Enable for Register 1
  //   R10i: Enable for Register 1
  //   R11i: Enable for Register 1
  //   R12i: Enable for Register 1
  //   R13i: Enable for Register 1
  //   R14i: Enable for Register 1
  //   R15i: Enable for Register 1
  //   R0i: Enable for Register 1
  //   LHO1i: Enable for Register 1
  //   LHO2i: Enable for Register 1
  //   LHO3i: Enable for Register 1
  //   LHO4i: Enable for Register 1
  //   LHO5i: Enable for Register 1
  //   LHO6i: Enable for Register 1
  //   LHO7i: Enable for Register 1
  //   LHO8i: Enable for Register 1
  //   LHO9i: Enable for Register 1
  //   LHO10i: Enable for Register 1
  //   LHO11i: Enable for Register 1
  //   LHO12i: Enable for Register 1
  //   LHO13i: Enable for Register 1
  //   LHO14i: Enable for Register 1
  //   LHO15i: Enable for Register 1
  //   LHO0i: Enable for Register 1
  //   RHO1i: Enable for Register 1
  //   RHO2i: Enable for Register 1
  //   RHO3i: Enable for Register 1
  //   RHO4i: Enable for Register 1
  //   RHO5i: Enable for Register 1
  //   RHO6i: Enable for Register 1
  //   RHO7i: Enable for Register 1
  //   RHO8i: Enable for Register 1
  //   RHO9i: Enable for Register 1
  //   RHO10i: Enable for Register 1
  //   RHO11i: Enable for Register 1
  //   RHO12i: Enable for Register 1
  //   RHO13i: Enable for Register 1
  //   RHO14i: Enable for Register 1
  //   RHO15i: Enable for Register 1
  //   RHO0i: Enable for Register 1
  //   Crement: Active to get the enabled register to
  //   do a "Crement" operation (inc/decrement)
  //   Which one occurs is dependent on Bit 5 of
  //   the register controller
  //   RCIi: Register Controller In inverted, default 1
  //   Bus: Bus data in
  //   Reset: Reset
  //   SI1: SPR index 1
  //   SI2: SPR index 2
  //   SPR: Use SPR instead of GPR
  //   SI3: SPR index 2
  //   SE1: SPR Enable 1
  //   SE2: SPR Enable 1
  //   SE3: SPR Enable 1
  //   SE4: SPR Enable 1
  //   SE5: SPR Enable 1
  //   SE6: SPR Enable 1
  //   SE7: SPR Enable 1
  //   SE8: SPR Enable 1
  //   SIO1: SPR Out index 1
  //   SIO2: SPR Out index 1
  //   SIO3: SPR Out index 1
  //   SOE1: SPR Output Enable 1
  //   SOE2: SPR Output Enable 1
  //   SOE3: SPR Output Enable 1
  //   SOE4: SPR Output Enable 1
  //   SOE5: SPR Output Enable 1
  //   SOE6: SPR Output Enable 1
  //   SOE7: SPR Output Enable 1
  //   SOE8: SPR Output Enable 1
  //   Left Hand Out Enable
  //   Right Hand Out Enable
  //   Only use the bottom 12/16
  //   bits of the main bus
  //   We use 12 bits to index the registers. Last 4 bits are the general
  //   register lines. The middle 4 are for the Right Hand output to the ALU
  //   First 4 are for the left hand side.
  //   Bit 5 is also used to tell the register to increment or decrement if the
  //   "Crement" control is sent, as these are mutually exclusive and
  //   only ever require the general enable of a register and never to the ALU
  //   Register Enable
endmodule
