// Digital circuit RegisterModule.dig as structural Verilog
module RegisterModule (
  input  OE,
  input  LHOEi,
  input  RHOEi,
  input  [15:0] IN,
  input  CLK,
  input  INC,
  input  DEC,
  input  Reset,
  input  Load,
  input  Enablei,
  input  [15:0] RHBusIn,
  input  RHIN,
  output [15:0] OUT,
  output [15:0] LHO,
  output [15:0] RHO
);

  wire _74193_1_pin12, _74193_1_pin13, _74193_2_pin12, _74193_2_pin13, _74193_3_pin12, _74193_3_pin13,
       and_1_out, and_2_out, and_3_out, nand_1_out, nand_2_out, nand_3_out, not_1_out, not_2_out, not_3_out,
       not_4_out, not_5_out, not_6_out;
  wire [15:0] _74193_1_pin7, _74193_1_pin15;

  not not_1 (not_1_out, Enablei);
  and and_1 (and_1_out, not_1_out, CLK);
  and and_2 (and_2_out, not_1_out, OE);
  not not_2 (not_2_out, and_1_out);
  nand nand_1 (nand_1_out, and_1_out, DEC);
  nand nand_2 (nand_2_out, INC, and_1_out);
  not not_3 (not_3_out, not_2_out);
  not not_4 (not_4_out, not_3_out);
  and and_3 (and_3_out, not_4_out, and_1_out);
  nand nand_3 (nand_3_out, and_3_out, Load);
  _74193 _74193_1 (
    .pin1(_74193_1_pin15[1]), .pin2(_74193_1_pin7[1]), .pin3(_74193_1_pin7[0]), .pin4(nand_1_out),
    .pin5(nand_2_out), .pin6(_74193_1_pin7[2]), .pin7(_74193_1_pin7[3]), .pin8(1'b0),
    .pin9(_74193_1_pin15[3]), .pin10(_74193_1_pin15[2]), .pin11(nand_3_out), .pin12(_74193_1_pin12),
    .pin13(_74193_1_pin13), .pin14(Reset), .pin15(_74193_1_pin15[0]), .pin16(1'b1));
  assign _74193_1_pin15 = RHIN ? RHBusIn : 16'bz;  // Driver driver_1
  assign _74193_1_pin15 = ~RHIN ? IN : 16'bz;  // DriverInvSel driverinvsel_1
  _74193 _74193_2 (
    .pin1(_74193_1_pin15[5]), .pin2(_74193_1_pin7[5]), .pin3(_74193_1_pin7[4]), .pin4(_74193_1_pin13),
    .pin5(_74193_1_pin12), .pin6(_74193_1_pin7[6]), .pin7(_74193_1_pin7[7]), .pin8(1'b0),
    .pin9(_74193_1_pin15[7]), .pin10(_74193_1_pin15[6]), .pin11(nand_3_out), .pin12(_74193_2_pin12),
    .pin13(_74193_2_pin13), .pin14(Reset), .pin15(_74193_1_pin15[4]), .pin16(1'b1));
  _74193 _74193_3 (
    .pin1(_74193_1_pin15[9]), .pin2(_74193_1_pin7[9]), .pin3(_74193_1_pin7[8]), .pin4(_74193_2_pin13),
    .pin5(_74193_2_pin12), .pin6(_74193_1_pin7[10]), .pin7(_74193_1_pin7[11]), .pin8(1'b0),
    .pin9(_74193_1_pin15[11]), .pin10(_74193_1_pin15[10]), .pin11(nand_3_out), .pin12(_74193_3_pin12),
    .pin13(_74193_3_pin13), .pin14(Reset), .pin15(_74193_1_pin15[8]), .pin16(1'b1));
  _74193 _74193_4 (
    .pin1(_74193_1_pin15[13]), .pin2(_74193_1_pin7[13]), .pin3(_74193_1_pin7[12]), .pin4(_74193_3_pin13),
    .pin5(_74193_3_pin12), .pin6(_74193_1_pin7[14]), .pin7(_74193_1_pin7[15]), .pin8(1'b0),
    .pin9(_74193_1_pin15[15]), .pin10(_74193_1_pin15[14]), .pin11(nand_3_out), .pin14(Reset),
    .pin15(_74193_1_pin15[12]), .pin16(1'b1));  // open: pin12, pin13
  not not_5 (not_5_out, LHOEi);
  not not_6 (not_6_out, RHOEi);
  assign LHO = not_5_out ? _74193_1_pin7 : 16'bz;  // Driver driver_2
  assign RHO = not_6_out ? _74193_1_pin7 : 16'bz;  // Driver driver_3
  assign OUT = and_2_out ? _74193_1_pin7 : 16'bz;  // Driver driver_4

  // Notes on the sheet:
  //   OE: Output Enable - If this register is Enabled and OE is brought High,
  //   the register will output its contents to the main bus
  //   LHOEi: Left Hand Output Enable inverted - If high, regardless of if this register is
  //   Enabled or not, this register will output it's contents to the Left Hand of the ALU
  //   OUT: The output to main bus
  //   Note that Main Bus In and Out should likely physically be the same
  //   RHOEi: Right Hand Output Enable inverted - If high, regardless of if this register is
  //   Enabled or not, this register will output it's contents to the right Hand of the ALU
  //   LHO: The output the left hand of the ALU
  //   RHO: Output to the Right Hand Bus.
  //   Note that Right Hand In and Out should likely physically be the same
  //   IN: Input from the Main Bus.
  //   Note that Main Bus In and Out should physically be the same
  //   INC: Increment on falling edge of clock pulse
  //   DEC: Decrements on falling edge of clock pulse
  //   Load: Loads data from bus on rising edge of clock pulse
  //   Enablei: Register Enable Inverted
  //   This is inverted because the output of the register controller is inverted, default 1
  //   RHBusIn: Input from the Right Hand Bus.
  //   This is used for move operations between 2 registers
  //   Note that Right Hand In and Out should likely physically be the same
  //   RHIN: Tells load to load from the right hand bus
  //   instead of main bus for register moving
  //   Bits 0-3
  //   Bits 4-7
  //   Bits 8-11
  //   Bits 12-15
endmodule
