// Logisim project NOS.circ as structural Verilog: 22 circuits, main circuit main
module main (
  input  [7:0] DataBusSet,
  input  in_2,
  input  [23:0] AddressBusSet,
  input  in_4,
  input  Manual,
  input  in_6,
  input  in_7,
  input  in_8,
  input  in_9,
  input  in_10,
  input  in_11,
  input  in_12,
  input  in_13,
  input  in_14,
  input  in_15,
  input  in_16,
  input  in_17,
  input  in_18,
  input  in_19,
  input  in_20,
  input  in_21,
  input  in_22,
  input  in_23,
  input  in_24,
  input  in_25,
  input  in_26,
  input  in_27,
  input  in_28,
  input  in_29,
  input  in_30,
  input  in_31,
  input  in_32,
  input  in_33,
  input  in_34,
  input  in_35,
  input  in_36,
  input  in_37,
  input  in_38,
  input  in_39,
  input  in_40,
  input  in_41,
  input  in_42,
  input  in_43,
  input  in_44,
  input  in_45,
  input  in_46,
  input  in_47,
  input  in_48,
  input  in_49,
  input  in_50,
  input  in_51,
  output [23:0] AddressBus,
  output [7:0] DataBus
);

  wire address_controller_1_add, address_controller_1_clko, address_controller_1_dataout,
       address_controller_1_fullload, address_controller_1_inc, address_controller_1_indexend,
       address_controller_1_load8, address_controller_1_reset, address_controller_2_add,
       address_controller_2_clko, address_controller_2_dataout, address_controller_2_fullload,
       address_controller_2_inc, address_controller_2_indexend, address_controller_2_load8,
       address_controller_2_reset, address_controller_3_clko, address_controller_3_dataout,
       address_controller_3_fullload, address_controller_3_inc, address_controller_3_indexend,
       address_controller_3_load8, address_controller_3_reset, address_module_1_zsout,
       address_module_2_zsout, address_module_3_clkout, address_module_3_in8o, address_module_3_loadfullo,
       address_module_3_outo, address_module_3_rc, address_module_3_resetout, address_module_3_zsout,
       address_module_4_clkout, address_module_4_in8o, address_module_4_loadfullo, address_module_4_outo,
       address_module_4_rc, address_module_4_resetout, address_module_4_zsout, address_module_5_zsout,
       address_module_6_clkout, address_module_6_in8o, address_module_6_loadfullo, address_module_6_outo,
       address_module_6_rc, address_module_6_resetout, address_module_6_zsout, address_module_7_clkout,
       address_module_7_in8o, address_module_7_loadfullo, address_module_7_outo, address_module_7_rc,
       address_module_7_resetout, alu_1_borrowout, alu_1_carryout, and_1_out, button_1_out, button_2_out,
       button_3_out, button_4_out, button_5_out, button_6_out, button_7_out, button_8_out, button_9_out,
       button_10_out, button_11_out, button_12_out, button_13_out, button_14_out, button_15_out,
       button_16_out, button_17_out, button_18_out, button_19_out, button_20_out, button_21_out, clock_1_out,
       controlled_buffer_1_out, instruction_controller_1_bro, instruction_controller_1_crm,
       instruction_controller_1_eii, instruction_controller_1_eo, instruction_controller_1_gr,
       instruction_controller_1_gro, instruction_controller_1_hlt, instruction_controller_1_mar,
       instruction_controller_1_pc, instruction_controller_1_pco, instruction_controller_1_rci,
       instruction_controller_1_ri, instruction_controller_1_rmi, instruction_controller_1_rmo,
       instruction_controller_1_ro, instruction_controller_1_ruc, manualcontrol_1_manual_mode_out,
       marfirstmodule_1_clkout, marfirstmodule_1_in8o, marfirstmodule_1_loadfullo, marfirstmodule_1_outo,
       marfirstmodule_1_rc, marfirstmodule_1_resetout, marfirstmodule_2_clkout, marfirstmodule_2_in8o,
       marfirstmodule_2_loadfullo, marfirstmodule_2_outo, marfirstmodule_2_rc, marfirstmodule_2_resetout,
       not_1_out, or_1_out, or_2_out, or_3_out, raminterface_keyboard_1_a1, raminterface_keyboard_1_a2,
       raminterface_keyboard_1_a3, raminterface_keyboard_1_a4, raminterface_keyboard_1_b1,
       raminterface_keyboard_1_b2, raminterface_keyboard_1_b3, raminterface_keyboard_1_b4,
       raminterface_keyboard_1_c1, raminterface_keyboard_1_c2, raminterface_keyboard_1_c3,
       raminterface_keyboard_1_c4, raminterface_keyboard_1_d1, raminterface_keyboard_1_d2,
       raminterface_keyboard_1_d3, raminterface_keyboard_1_d4, raminterface_keyboard_1_e1,
       raminterface_keyboard_1_e2, raminterface_keyboard_1_e3, raminterface_keyboard_1_e4,
       raminterface_keyboard_1_f1, raminterface_keyboard_1_f2, raminterface_keyboard_1_f3,
       raminterface_keyboard_1_f4, raminterface_keyboard_1_g1, raminterface_keyboard_1_g2,
       raminterface_keyboard_1_g3, raminterface_keyboard_1_g4, raminterface_keyboard_1_ramclk,
       raminterface_keyboard_1_ramout, raminterface_keyboard_1_ramwrite, register_controller_1_borrowresult,
       register_controller_1_carryresult, register_controller_1_enable0i, register_controller_1_lho0i,
       register_controller_1_output0i, register_controller_1_rho0i, register_module_1_p2,
       register_module_1_p3, register_module_1_p4, register_module_1_p5, register_module_1_p6,
       register_module_1_p7, register_module_1_p8, register_module_1_p12, register_module_1_p13,
       register_module_1_p14, register_module_1_p15, register_module_1_p16, register_module_1_p17, Reset_out;
  wire [3:0] instruction_controller_1_stepout;
  wire [7:0] address_controller_1_idout, address_controller_2_idout, address_controller_3_idout,
       address_module_1_out8out, address_module_2_out8out, address_module_3_addressout,
       address_module_3_idout, address_module_3_out8out, address_module_4_addressout, address_module_4_idout,
       address_module_4_out8out, address_module_5_out8out, address_module_6_addressout,
       address_module_6_idout, address_module_6_out8out, address_module_7_addressout, address_module_7_idout,
       address_module_7_out8out, instruction_controller_1_instruction, marfirstmodule_1_addressout,
       marfirstmodule_1_idout, marfirstmodule_1_out8out, marfirstmodule_2_addressout, marfirstmodule_2_idout,
       marfirstmodule_2_out8out, ram_module_1_dataout, raminterface_keyboard_1_ramdatain,
       register_module_1_p1, register_module_1_p9, register_module_1_p10, register_module_1_p11;
  wire [8:0] instruction_controller_1_iid;
  wire [15:0] marfirstmodule_2_value, raminterface_keyboard_1_ramaddress;
  wire [43:0] manualcontrol_1_out_46;
  wire [47:0] eeprom_decoder_1_decodedinst;

  Button button_1 (.out(button_1_out));
  Button button_2 (.out(button_2_out));
  Button button_3 (.out(button_3_out));
  Button button_4 (.out(button_4_out));
  Button button_5 (.out(button_5_out));
  Button button_6 (.out(button_6_out));
  Button button_7 (.out(button_7_out));
  Button button_8 (.out(button_8_out));
  Button button_9 (.out(button_9_out));
  Button button_10 (.out(button_10_out));
  Button button_11 (.out(button_11_out));
  Button button_12 (.out(button_12_out));
  Button button_13 (.out(button_13_out));
  Button button_14 (.out(button_14_out));
  Button button_15 (.out(button_15_out));
  Button button_16 (.out(button_16_out));
  _7_Segment_Display u_7_segment_display_1 (
    .g(raminterface_keyboard_1_g4), .f(raminterface_keyboard_1_f4), .a(raminterface_keyboard_1_a4),
    .b(raminterface_keyboard_1_b4), .e(raminterface_keyboard_1_e4), .d(raminterface_keyboard_1_d4),
    .c(raminterface_keyboard_1_c4));  // open: dp
  _7_Segment_Display u_7_segment_display_2 (
    .g(raminterface_keyboard_1_g3), .f(raminterface_keyboard_1_f3), .a(raminterface_keyboard_1_a3),
    .b(raminterface_keyboard_1_b3), .e(raminterface_keyboard_1_e3), .d(raminterface_keyboard_1_d3),
    .c(raminterface_keyboard_1_c3));  // open: dp
  _7_Segment_Display u_7_segment_display_3 (
    .g(raminterface_keyboard_1_g2), .f(raminterface_keyboard_1_f2), .a(raminterface_keyboard_1_a2),
    .b(raminterface_keyboard_1_b2), .e(raminterface_keyboard_1_e2), .d(raminterface_keyboard_1_d2),
    .c(raminterface_keyboard_1_c2));  // open: dp
  RAM_Module ram_module_1 (
    .DataOut(ram_module_1_dataout), .Write(raminterface_keyboard_1_ramwrite),
    .CLK(raminterface_keyboard_1_ramclk), .DataIn(raminterface_keyboard_1_ramdatain),
    .Out(raminterface_keyboard_1_ramout), .Address(raminterface_keyboard_1_ramaddress));
  not not_1 (not_1_out, Manual);
  assign controlled_buffer_1_out = Manual ? button_17_out : 1'bz;  // Controlled_Buffer controlled_buffer_1
  Button button_17 (.out(button_17_out));
  _7_Segment_Display u_7_segment_display_4 (
    .g(raminterface_keyboard_1_g1), .f(raminterface_keyboard_1_f1), .a(raminterface_keyboard_1_a1),
    .b(raminterface_keyboard_1_b1), .e(raminterface_keyboard_1_e1), .d(raminterface_keyboard_1_d1),
    .c(raminterface_keyboard_1_c1));  // open: dp
  Clock clock_1 (.out(clock_1_out));
  assign controlled_buffer_1_out = not_1_out ? clock_1_out : 1'bz;  // Controlled_Buffer controlled_buffer_2
  and and_1 (and_1_out, controlled_buffer_1_out, instruction_controller_1_hlt);
  Button button_18 (.out(button_18_out));
  Button button_19 (.out(button_19_out));
  Address_Module address_module_1 (
    .ZSOut(address_module_1_zsout), .Out8Out(address_module_1_out8out), .Value(AddressBus[23:16]),
    .Clk(address_module_3_clkout), .IDIn(address_module_3_idout), .LoadFull(address_module_3_loadfullo),
    .Reset(address_module_3_resetout), .In8(address_module_3_in8o), .Inc(address_module_3_rc),
    .AddressIn(address_module_3_addressout), .AddressBusIn(AddressBus[23:16]), .OutI(address_module_3_outo));  // open: ClkOut, IDOut, LoadFullO, ResetOut, In8O, OutO, AddressOut, RC, ZSIn, Out8In
  Button button_20 (.out(button_20_out));
  Button button_21 (.out(button_21_out));
  Address_Module address_module_2 (
    .ZSOut(address_module_2_zsout), .Out8Out(address_module_2_out8out), .Clk(address_module_4_clkout),
    .IDIn(address_module_4_idout), .LoadFull(address_module_4_loadfullo), .Reset(address_module_4_resetout),
    .In8(address_module_4_in8o), .Inc(address_module_4_rc), .AddressIn(address_module_4_addressout),
    .AddressBusIn(AddressBus[23:16]), .OutI(address_module_4_outo));  // open: ClkOut, IDOut, LoadFullO, ResetOut, In8O, Value, OutO, AddressOut, RC, ZSIn, Out8In
  Address_Module address_module_3 (
    .ClkOut(address_module_3_clkout), .IDOut(address_module_3_idout), .LoadFullO(address_module_3_loadfullo),
    .ResetOut(address_module_3_resetout), .In8O(address_module_3_in8o), .ZSOut(address_module_3_zsout),
    .Out8Out(address_module_3_out8out), .Value(AddressBus[15:8]), .OutO(address_module_3_outo),
    .AddressOut(address_module_3_addressout), .RC(address_module_3_rc), .Clk(marfirstmodule_1_clkout),
    .IDIn(marfirstmodule_1_idout), .LoadFull(marfirstmodule_1_loadfullo), .Reset(marfirstmodule_1_resetout),
    .In8(marfirstmodule_1_in8o), .Inc(marfirstmodule_1_rc), .AddressIn(marfirstmodule_1_addressout),
    .AddressBusIn(AddressBus[15:8]), .ZSIn(address_module_1_zsout), .OutI(marfirstmodule_1_outo),
    .Out8In(address_module_1_out8out));
  MARFirstModule marfirstmodule_1 (
    .ClkOut(marfirstmodule_1_clkout), .IDOut(marfirstmodule_1_idout), .LoadFullO(marfirstmodule_1_loadfullo),
    .ResetOut(marfirstmodule_1_resetout), .In8O(marfirstmodule_1_in8o), .Out8Out(marfirstmodule_1_out8out),
    .Value(AddressBus[7:0]), .OutO(marfirstmodule_1_outo), .AddressOut(marfirstmodule_1_addressout),
    .RC(marfirstmodule_1_rc), .Clk(address_controller_1_clko), .IDIn(address_controller_1_idout),
    .LoadFull(address_controller_1_fullload), .Reset(address_controller_1_reset),
    .In8(address_controller_1_load8), .Inc(address_controller_1_inc), .AddressBusIn(AddressBus[7:0]),
    .AddressIn(DataBus), .ZSIn(address_module_3_zsout), .ADD(address_controller_1_add),
    .OutI(address_controller_1_dataout), .Out8In(address_module_3_out8out));  // open: ZSOut
  Address_Controller address_controller_1 (
    .Load8(address_controller_1_load8), .FullLoad(address_controller_1_fullload),
    .Inc(address_controller_1_inc), .Add(address_controller_1_add), .DataOut(address_controller_1_dataout),
    .Data8Out(DataBus), .ClkO(address_controller_1_clko), .Reset(address_controller_1_reset),
    .IDOut(address_controller_1_idout), .IndexEnd(address_controller_1_indexend),
    .RegisterOps(instruction_controller_1_iid), .EnableRegister(instruction_controller_1_gr),
    .RegOut(instruction_controller_1_gro), .IDIn(DataBus), .Data8In(marfirstmodule_1_out8out),
    .Clk(and_1_out), .MasterReset(Reset_out));
  Address_Module address_module_4 (
    .ClkOut(address_module_4_clkout), .IDOut(address_module_4_idout), .LoadFullO(address_module_4_loadfullo),
    .ResetOut(address_module_4_resetout), .In8O(address_module_4_in8o), .ZSOut(address_module_4_zsout),
    .Out8Out(address_module_4_out8out), .Value(marfirstmodule_2_value[15:8]), .OutO(address_module_4_outo),
    .AddressOut(address_module_4_addressout), .RC(address_module_4_rc), .Clk(marfirstmodule_2_clkout),
    .IDIn(marfirstmodule_2_idout), .LoadFull(marfirstmodule_2_loadfullo), .Reset(marfirstmodule_2_resetout),
    .In8(marfirstmodule_2_in8o), .Inc(marfirstmodule_2_rc), .AddressIn(marfirstmodule_2_addressout),
    .AddressBusIn(AddressBus[15:8]), .ZSIn(address_module_2_zsout), .OutI(marfirstmodule_2_outo),
    .Out8In(address_module_2_out8out));
  MARFirstModule marfirstmodule_2 (
    .ClkOut(marfirstmodule_2_clkout), .IDOut(marfirstmodule_2_idout), .LoadFullO(marfirstmodule_2_loadfullo),
    .ResetOut(marfirstmodule_2_resetout), .In8O(marfirstmodule_2_in8o), .Out8Out(marfirstmodule_2_out8out),
    .Value(marfirstmodule_2_value[7:0]), .OutO(marfirstmodule_2_outo),
    .AddressOut(marfirstmodule_2_addressout), .RC(marfirstmodule_2_rc), .Clk(address_controller_2_clko),
    .IDIn(address_controller_2_idout), .LoadFull(address_controller_2_fullload),
    .Reset(address_controller_2_reset), .In8(address_controller_2_load8), .Inc(address_controller_2_inc),
    .AddressBusIn(AddressBus[7:0]), .AddressIn(DataBus), .ZSIn(address_module_4_zsout),
    .ADD(address_controller_2_add), .OutI(address_controller_2_dataout), .Out8In(address_module_4_out8out));  // open: ZSOut
  Address_Controller address_controller_2 (
    .Load8(address_controller_2_load8), .FullLoad(address_controller_2_fullload),
    .Inc(address_controller_2_inc), .Add(address_controller_2_add), .DataOut(address_controller_2_dataout),
    .Data8Out(DataBus), .ClkO(address_controller_2_clko), .Reset(address_controller_2_reset),
    .IDOut(address_controller_2_idout), .IndexEnd(address_controller_2_indexend),
    .RegisterOps(instruction_controller_1_iid), .EnableRegister(instruction_controller_1_mar), .RegOut(1'b1),
    .IDIn(DataBus), .Data8In(marfirstmodule_2_out8out), .Clk(and_1_out), .MasterReset(Reset_out));
  RAMInterface_Keyboard raminterface_keyboard_1 (
    .RAMDataIn(raminterface_keyboard_1_ramdatain), .A3(raminterface_keyboard_1_a3),
    .B3(raminterface_keyboard_1_b3), .C3(raminterface_keyboard_1_c3), .D3(raminterface_keyboard_1_d3),
    .E3(raminterface_keyboard_1_e3), .F3(raminterface_keyboard_1_f3), .G3(raminterface_keyboard_1_g3),
    .A4(raminterface_keyboard_1_a4), .B4(raminterface_keyboard_1_b4), .C4(raminterface_keyboard_1_c4),
    .D4(raminterface_keyboard_1_d4), .E4(raminterface_keyboard_1_e4), .F4(raminterface_keyboard_1_f4),
    .G4(raminterface_keyboard_1_g4), .RAMAddress(raminterface_keyboard_1_ramaddress),
    .A2(raminterface_keyboard_1_a2), .B2(raminterface_keyboard_1_b2), .C2(raminterface_keyboard_1_c2),
    .D2(raminterface_keyboard_1_d2), .E2(raminterface_keyboard_1_e2), .F2(raminterface_keyboard_1_f2),
    .G2(raminterface_keyboard_1_g2), .RAMOut(raminterface_keyboard_1_ramout),
    .RAMWrite(raminterface_keyboard_1_ramwrite), .RAMClk(raminterface_keyboard_1_ramclk),
    .DataBusOut(DataBus), .A1(raminterface_keyboard_1_a1), .B1(raminterface_keyboard_1_b1),
    .C1(raminterface_keyboard_1_c1), .D1(raminterface_keyboard_1_d1), .E1(raminterface_keyboard_1_e1),
    .F1(raminterface_keyboard_1_f1), .G1(raminterface_keyboard_1_g1), .DecAddress(button_21_out),
    .IncAddress(button_19_out), .Manual(in_6), .MARIn(marfirstmodule_2_value), .DataBusIn(DataBus),
    .BUTTON_9(button_11_out), .BUTTON_10(button_12_out), .BUTTON_11(button_13_out), .BUTTON_12(button_4_out),
    .BUTTON_13(button_14_out), .BUTTON_14(button_15_out), .BUTTON_15(button_16_out), .TYPE_ADDRESS(in_7),
    .BUTTON_0(button_1_out), .BUTTON_1(button_5_out), .BUTTON_2(button_6_out), .BUTTON_3(button_7_out),
    .BUTTON_4(button_2_out), .BUTTON_5(button_8_out), .BUTTON_6(button_9_out), .BUTTON_7(button_10_out),
    .BUTTON_8(button_3_out), .OutValue(button_18_out), .DataOut(instruction_controller_1_rmo),
    .WE(instruction_controller_1_rmi), .CLK(and_1_out), .WriteValue(button_20_out),
    .RAMDataOut(ram_module_1_dataout));
  assign AddressBus = in_4 ? AddressBusSet : 24'bz;  // Controlled_Buffer controlled_buffer_3
  Pull_Resistor pull_resistor_1 (.node(AddressBus));
  assign DataBus = in_2 ? DataBusSet : 8'bz;  // Controlled_Buffer controlled_buffer_4
  Pull_Resistor pull_resistor_2 (.node(DataBus));
  or or_1 (or_1_out, address_controller_1_indexend, or_2_out);
  Button Reset (.out(Reset_out));
  Address_Module address_module_5 (
    .ZSOut(address_module_5_zsout), .Out8Out(address_module_5_out8out), .Value(AddressBus[23:16]),
    .Clk(address_module_6_clkout), .IDIn(address_module_6_idout), .LoadFull(address_module_6_loadfullo),
    .Reset(address_module_6_resetout), .In8(address_module_6_in8o), .Inc(address_module_6_rc),
    .AddressIn(address_module_6_addressout), .AddressBusIn(AddressBus[23:16]), .OutI(address_module_6_outo));  // open: ClkOut, IDOut, LoadFullO, ResetOut, In8O, OutO, AddressOut, RC, ZSIn, Out8In
  // Register_Module register_module_1: pin names not known; wires that end beside it: register_module_1_p1, register_module_1_p2, register_module_1_p3, register_module_1_p4, register_module_1_p5, register_module_1_p6, register_module_1_p7, register_module_1_p8, register_module_1_p9, register_module_1_p10, register_module_1_p11, register_module_1_p12, register_module_1_p13, register_module_1_p14, register_module_1_p15, register_module_1_p16, register_module_1_p17
  or or_2 (or_2_out, address_controller_2_indexend, address_controller_3_indexend);
  Register_Module register_module_2 (
    .DataOut(register_module_1_p9), .LHO(register_module_1_p10), .RHO(register_module_1_p11),
    .CarryOut(register_module_1_p12), .BorrowOut(register_module_1_p13), .Load(register_module_1_p2),
    .Dec(register_module_1_p5), .Inc(register_module_1_p4), .Clk(register_module_1_p7),
    .Enablei(register_controller_1_enable0i), .BypassOuti(register_controller_1_output0i),
    .OE(register_module_1_p3), .LHSE(register_controller_1_lho0i), .RHSE(register_controller_1_rho0i),
    .Data(register_module_1_p1), .Reset(register_module_1_p8), .Carry(register_module_1_p6));
  Register_Controller register_controller_1 (
    .CLKOut(register_module_1_p7), .Load(register_module_1_p2), .Reset(register_module_1_p8),
    .OE(register_module_1_p3), .DataBusIn(register_module_1_p1),
    .CarryResult(register_controller_1_carryresult), .BorrowResult(register_controller_1_borrowresult),
    .DataBusOut(DataBus), .Inc(register_module_1_p4), .Dec(register_module_1_p5),
    .CarryToReg(register_module_1_p6), .Output0i(register_controller_1_output0i),
    .Output1i(register_module_1_p17), .RHO0i(register_controller_1_rho0i), .RHO1i(register_module_1_p14),
    .LHO0i(register_controller_1_lho0i), .LHO1i(register_module_1_p15),
    .Enable0i(register_controller_1_enable0i), .Enable1i(register_module_1_p16), .CLK(and_1_out),
    .RIn(instruction_controller_1_ri), .RReset(Reset_out), .ROut(instruction_controller_1_ro),
    .DataBus(DataBus), .RControllerIn(instruction_controller_1_rci),
    .BypassedOuti(instruction_controller_1_bro), .CarryIn(instruction_controller_1_ruc),
    .Crement(instruction_controller_1_crm), .RegisterCarry(register_module_1_p12),
    .RegisterBorrow(register_module_1_p13), .RegisterBusOut(register_module_1_p9));  // open: Output2i, Output3i, RHO2i, RHO3i, LHO2i, LHO3i, Enable2i, Enable3i
  Address_Module address_module_6 (
    .ClkOut(address_module_6_clkout), .IDOut(address_module_6_idout), .LoadFullO(address_module_6_loadfullo),
    .ResetOut(address_module_6_resetout), .In8O(address_module_6_in8o), .ZSOut(address_module_6_zsout),
    .Out8Out(address_module_6_out8out), .Value(AddressBus[15:8]), .OutO(address_module_6_outo),
    .AddressOut(address_module_6_addressout), .RC(address_module_6_rc), .Clk(address_module_7_clkout),
    .IDIn(address_module_7_idout), .LoadFull(address_module_7_loadfullo), .Reset(address_module_7_resetout),
    .In8(address_module_7_in8o), .Inc(address_module_7_rc), .AddressIn(address_module_7_addressout),
    .AddressBusIn(AddressBus[15:8]), .ZSIn(address_module_5_zsout), .OutI(address_module_7_outo),
    .Out8In(address_module_5_out8out));
  Address_Module address_module_7 (
    .ClkOut(address_module_7_clkout), .IDOut(address_module_7_idout), .LoadFullO(address_module_7_loadfullo),
    .ResetOut(address_module_7_resetout), .In8O(address_module_7_in8o), .Out8Out(address_module_7_out8out),
    .Value(AddressBus[7:0]), .OutO(address_module_7_outo), .AddressOut(address_module_7_addressout),
    .RC(address_module_7_rc), .Clk(address_controller_3_clko), .IDIn(address_controller_3_idout),
    .LoadFull(address_controller_3_fullload), .Reset(address_controller_3_reset),
    .In8(address_controller_3_load8), .Inc(address_controller_3_inc), .AddressIn(DataBus),
    .AddressBusIn(AddressBus[7:0]), .ZSIn(address_module_6_zsout), .OutI(address_controller_3_dataout),
    .Out8In(address_module_6_out8out));  // open: ZSOut
  Address_Controller address_controller_3 (
    .Load8(address_controller_3_load8), .FullLoad(address_controller_3_fullload),
    .Inc(address_controller_3_inc), .DataOut(address_controller_3_dataout), .Data8Out(DataBus),
    .ClkO(address_controller_3_clko), .Reset(address_controller_3_reset), .IDOut(address_controller_3_idout),
    .IndexEnd(address_controller_3_indexend), .RegisterOps(instruction_controller_1_iid),
    .EnableRegister(instruction_controller_1_pc), .RegOut(instruction_controller_1_pco), .IDIn(DataBus),
    .Data8In(address_module_7_out8out), .Clk(and_1_out), .MasterReset(Reset_out));  // open: Add
  LED led_1 (.in(register_controller_1_carryresult));
  LED led_2 (.in(register_controller_1_borrowresult));
  Instruction_Controller instruction_controller_1 (
    .StepOut(instruction_controller_1_stepout), .Instruction(instruction_controller_1_instruction),
    .DataOut(DataBus), .HLT(instruction_controller_1_hlt), .RCI(instruction_controller_1_rci),
    .RI(instruction_controller_1_ri), .RO(instruction_controller_1_ro), .RUC(instruction_controller_1_ruc),
    .CRM(instruction_controller_1_crm), .BRO(instruction_controller_1_bro),
    .IID(instruction_controller_1_iid[0]), .DID(instruction_controller_1_iid[1]),
    .IDI(instruction_controller_1_iid[2]), .OUT8(instruction_controller_1_iid[3]),
    .IN8(instruction_controller_1_iid[4]), .FLOD(instruction_controller_1_iid[5]),
    .IR(instruction_controller_1_iid[6]), .ADR(instruction_controller_1_iid[8]),
    .RSR(instruction_controller_1_iid[7]), .MAR(instruction_controller_1_mar),
    .PC(instruction_controller_1_pc), .PCO(instruction_controller_1_pco), .GR(instruction_controller_1_gr),
    .GRO(instruction_controller_1_gro), .RMO(instruction_controller_1_rmo),
    .RMI(instruction_controller_1_rmi), .EO(instruction_controller_1_eo), .EII(instruction_controller_1_eii),
    .CLK(and_1_out), .DataBus(DataBus), .ExpansionControl(manualcontrol_1_manual_mode_out),
    .Decoded_Instruction(eeprom_decoder_1_decodedinst[43:0]),
    .Control_Line_Expansion(manualcontrol_1_out_46), .Reset(Reset_out), .ESC(or_3_out));  // open: FSI, SF, CF, LF, FO, DFI, PSH, POP, IOI, IOO, IDO, SID
  or or_3 (or_3_out, or_1_out, Reset_out);
  EEPROM_Decoder eeprom_decoder_1 (
    .DecodedInst(eeprom_decoder_1_decodedinst), .Step(instruction_controller_1_stepout),
    .Instruction(instruction_controller_1_instruction));
  ALU alu_1 (
    .DataOut(DataBus), .CarryOut(alu_1_carryout), .BorrowOut(alu_1_borrowout),
    .InstrIn(instruction_controller_1_eii), .CLK(and_1_out), .Instruction(DataBus),
    .RightHandIn(register_module_1_p11), .LeftHandIn(register_module_1_p10), .CarryIn(1'b0),
    .EO(instruction_controller_1_eo));  // open: out_18, out_19, ClockLine, EnableLine, ShiftLeft, ShiftRight, RotL, RotR, Carry
  LED led_3 (.in(alu_1_carryout));
  LED led_4 (.in(alu_1_borrowout));
  ManualControl manualcontrol_1 (
    .Manual_Mode_Out(manualcontrol_1_manual_mode_out), .out_46(manualcontrol_1_out_46), .Manual_Mode(in_30),
    .DFI(in_43), .EO(in_44), .EII(in_45), .PSH(in_46), .POP(in_47), .IOI(in_48), .IOO(in_49), .IDO(in_50),
    .SID(in_51), .HLT(in_8), .RCI(in_9), .RI(in_10), .RO(in_11), .RUC(in_12), .CRM(in_13), .SFT(in_14),
    .ROT(in_15), .NOTc(in_16), .BRO(in_17), .IID(in_18), .DID(in_19), .IDI(in_20), .OUT8(in_21), .IN8(in_22),
    .FLOD(in_23), .IR(in_24), .ADR(in_25), .RSR(in_26), .MAR(in_27), .PC(in_28), .PCO(in_29), .GR(in_31),
    .GRO(in_32), .RMO(in_33), .RMI(in_34), .IRI(in_35), .IRO(in_36), .SCR(in_37), .FSI(in_38), .SF(in_39),
    .CF(in_40), .LF(in_41), .FO(in_42));

  // Notes on the sheet:
  //   0
  //   1
  //   4
  //   5
  //   8
  //   9
  //   C
  //   D
  //   2
  //   3
  //   6
  //   7
  //   A
  //   B
  //   E
  //   F
  //   GAR
  //   MAR
  //   PC
endmodule

module HCT139_2to4LineDecoder (
  input  G1i,
  input  A1,
  input  B1,
  input  G2i,
  input  A2,
  input  B2,
  output Y10,
  output Y11,
  output Y12,
  output Y13,
  output Y20,
  output Y21,
  output Y22,
  output Y23
);

  wire not_1_out, not_2_out, not_3_out, not_4_out, not_5_out, not_6_out, not_7_out, not_8_out;

  not not_1 (not_1_out, G1i);
  not not_2 (not_2_out, A1);
  not not_3 (not_3_out, A1);
  not not_4 (not_4_out, B1);
  not not_5 (not_5_out, G2i);
  not not_6 (not_6_out, A2);
  not not_7 (not_7_out, A2);
  not not_8 (not_8_out, B2);
  nand nand_1 (Y10, not_1_out, not_2_out, not_4_out);
  nand nand_2 (Y11, not_1_out, A1, not_4_out);
  nand nand_3 (Y12, not_1_out, not_3_out, B1);
  nand nand_4 (Y13, not_1_out, A1, B1);
  nand nand_5 (Y20, not_5_out, not_6_out, not_8_out);
  nand nand_6 (Y21, not_5_out, A2, not_8_out);
  nand nand_7 (Y22, not_5_out, not_7_out, B2);
  nand nand_8 (Y23, not_5_out, A2, B2);
endmodule

module HC153_4To1MultiPlexer (
  input  E1i,
  input  D13,
  input  D12,
  input  D11,
  input  D10,
  input  S0,
  input  S1,
  input  D23,
  input  D22,
  input  D21,
  input  D20,
  input  E2i,
  output Y1,
  output Y2
);

  wire and_1_out, and_2_out, and_3_out, and_4_out, and_5_out, and_6_out, and_7_out, and_8_out, not_1_out,
       not_2_out, not_3_out, not_4_out, not_5_out, not_6_out;

  not not_1 (not_1_out, E1i);
  and and_1 (and_1_out, not_1_out, not_5_out, not_3_out, D13);
  and and_2 (and_2_out, not_1_out, not_2_out, not_5_out, D12);
  or or_1 (Y1, and_1_out, and_2_out, and_3_out, and_4_out);
  and and_3 (and_3_out, not_1_out, not_3_out, not_4_out, D11);
  and and_4 (and_4_out, not_1_out, not_2_out, not_4_out, D10);
  not not_2 (not_2_out, S0);
  not not_3 (not_3_out, not_2_out);
  not not_4 (not_4_out, S1);
  not not_5 (not_5_out, not_4_out);
  and and_5 (and_5_out, D23, not_3_out, not_5_out, not_6_out);
  and and_6 (and_6_out, D22, not_2_out, not_5_out, not_6_out);
  and and_7 (and_7_out, D21, not_4_out, not_3_out, not_6_out);
  or or_2 (Y2, and_5_out, and_6_out, and_7_out, and_8_out);
  not not_6 (not_6_out, E2i);
  and and_8 (and_8_out, D20, not_2_out, not_4_out, not_6_out);
endmodule

module HCT157_SelctorMultiplexer (
  input  [3:0] A,
  input  [3:0] B,
  input  S,
  input  Ei,
  output [3:0] Y
);

  wire not_1_out;

  Multiplexer #(.width(4)) multiplexer_1 (.in0(A), .in1(B), .out(Y), .sel(S), .en(not_1_out));
  not not_1 (not_1_out, Ei);
endmodule

module HCT173_QuadDTypeFF (
  input  OEi,
  input  [3:0] D,
  input  WEi,
  input  Clk,
  input  MR,
  output [3:0] Q
);

  wire not_1_out, not_2_out;
  wire [3:0] register_1_q;

  Register #(.width(4)) register_1 (.D(D), .en(not_2_out), .clk(Clk), .Q(register_1_q), .clr(MR));
  not not_1 (not_1_out, OEi);
  not not_2 (not_2_out, WEi);
  assign Q = not_1_out ? register_1_q : 4'bz;  // Controlled_Buffer controlled_buffer_1
endmodule

module HCT193_UpDownCounter (
  input  P0,
  input  P1,
  input  P2,
  input  P3,
  input  PLi,
  input  CPUi,
  input  CPDi,
  input  MR,
  output TCUi,
  output TCDi,
  output Q0,
  output Q1,
  output Q2,
  output Q3
);

  wire and_1_out, and_2_out, and_3_out, and_4_out, and_5_out, and_6_out, nand_1_out, nand_2_out, nand_3_out,
       nand_4_out, nand_5_out, nand_6_out, nand_7_out, nand_8_out, nor_1_out, nor_2_out, nor_3_out,
       nor_4_out, not_1_out, not_2_out, not_3_out, not_4_out, not_5_out, not_6_out, not_7_out, not_8_out,
       or_1_out, or_2_out, or_3_out, or_4_out, t_ff_1_qn, t_ff_2_qn, t_ff_3_qn, t_ff_4_qn;

  not not_1 (not_1_out, PLi);
  not not_2 (not_2_out, CPUi);
  not not_3 (not_3_out, CPDi);
  not not_4 (not_4_out, MR);
  nand nand_1 (nand_1_out, not_1_out, not_4_out, P0);
  not not_5 (not_5_out, nand_1_out);
  T_Flip_Flop t_ff_1 (.T(nor_1_out), .clk(nor_1_out), .Q(Q0), .Qn(t_ff_1_qn), .reset(or_1_out), .preset(not_5_out));
  nor nor_1 (nor_1_out, not_2_out, not_3_out);
  or or_1 (or_1_out, ~not_4_out, ~nand_2_out);  // OR_Gate
  nand nand_2 (nand_2_out, nand_1_out, not_1_out);
  and and_1 (and_1_out, not_2_out, Q0);
  and and_2 (and_2_out, t_ff_1_qn, not_3_out);
  nand nand_3 (nand_3_out, not_1_out, not_4_out, P1);
  not not_6 (not_6_out, nand_3_out);
  T_Flip_Flop t_ff_2 (.T(nor_2_out), .clk(nor_2_out), .Q(Q1), .Qn(t_ff_2_qn), .reset(or_2_out), .preset(not_6_out));
  nor nor_2 (nor_2_out, and_1_out, and_2_out);
  or or_2 (or_2_out, ~not_4_out, ~nand_4_out);  // OR_Gate
  nand nand_4 (nand_4_out, nand_3_out, not_1_out);
  and and_3 (and_3_out, not_2_out, Q0, Q1);
  nor nor_3 (nor_3_out, and_3_out, and_4_out);
  and and_4 (and_4_out, t_ff_2_qn, t_ff_1_qn, not_3_out);
  nand nand_5 (nand_5_out, not_1_out, not_4_out, P2);
  nand nand_6 (nand_6_out, nand_5_out, not_1_out);
  not not_7 (not_7_out, nand_5_out);
  T_Flip_Flop t_ff_3 (.T(nor_3_out), .clk(nor_3_out), .Q(Q2), .Qn(t_ff_3_qn), .reset(or_3_out), .preset(not_7_out));
  or or_3 (or_3_out, ~not_4_out, ~nand_6_out);  // OR_Gate
  and and_5 (and_5_out, not_2_out, Q1, Q0, Q2);
  and and_6 (and_6_out, t_ff_3_qn, t_ff_2_qn, t_ff_1_qn, not_3_out);
  T_Flip_Flop t_ff_4 (.T(nor_4_out), .clk(nor_4_out), .Q(Q3), .Qn(t_ff_4_qn), .reset(or_4_out), .preset(not_8_out));
  nor nor_4 (nor_4_out, and_5_out, and_6_out);
  nand nand_7 (nand_7_out, not_1_out, not_4_out, P3);
  nand nand_8 (nand_8_out, nand_7_out, not_1_out);
  not not_8 (not_8_out, nand_7_out);
  or or_4 (or_4_out, ~not_4_out, ~nand_8_out);  // OR_Gate
  nand nand_9 (TCUi, not_2_out, Q2, Q1, Q0, Q3);
  nand nand_10 (TCDi, not_3_out, t_ff_1_qn, t_ff_2_qn, t_ff_3_qn, t_ff_4_qn);
endmodule

module HCT283_Adder (
  input  CIn,
  input  [3:0] A,
  input  [3:0] B,
  output [3:0] S,
  output COut
);

  Adder #(.width(4)) adder_1 (.a(A), .b(B), .out(S), .cin(CIn), .cout(COut));
endmodule

module HCT574_OctalLatch (
  input  OEi,
  input  [7:0] D,
  input  CP,
  output [7:0] Q
);

  wire not_1_out;
  wire [7:0] register_1_q;

  Register register_1 (.D(D), .en(1'b1), .clk(CP), .Q(register_1_q), .clr(1'b0));
  not not_1 (not_1_out, OEi);
  assign Q = not_1_out ? register_1_q : 8'bz;  // Controlled_Buffer controlled_buffer_1
endmodule

module CY7C199_SRAM (
  input  [7:0] Input,
  input  [14:0] Address,
  input  WEi,
  input  CEi,
  input  OEi,
  output [7:0] Output
);

  wire and_1_out, and_2_out, not_1_out;
  wire [7:0] ram_1_data;

  and and_1 (and_1_out, ~WEi, ~CEi);  // AND_Gate
  and and_2 (and_2_out, ~CEi, ~OEi);  // AND_Gate
  RAM #(.addrWidth(15), .asyncread("true"), .databus("bidir")) ram_1 (
    .addr(Address), .we(and_1_out), .oe(and_2_out), .clk(and_1_out), .data(ram_1_data));
  assign ram_1_data = not_1_out ? Input : 8'bz;  // Controlled_Buffer controlled_buffer_1
  not not_1 (not_1_out, and_2_out);
  assign Output = and_2_out ? ram_1_data : 8'bz;  // Controlled_Buffer controlled_buffer_2
endmodule

module RAM_Module (
  input  [15:0] Address,
  input  [7:0] DataIn,
  input  Out,
  input  Write,
  input  CLK,
  output [7:0] DataOut
);

  wire and_1_out, and_2_out, not_1_out, not_2_out, not_3_out, not_4_out, not_5_out, not_6_out, not_7_out;
  wire [7:0] controlled_buffer_1_out;

  not not_1 (not_1_out, Out);
  not not_2 (not_2_out, CLK);
  assign controlled_buffer_1_out = not_3_out ? DataIn : 8'bz;  // Controlled_Buffer controlled_buffer_1
  not not_3 (not_3_out, Out);
  assign DataOut = Out ? controlled_buffer_1_out : 8'bz;  // Controlled_Buffer controlled_buffer_2
  and and_1 (and_1_out, CLK, not_5_out);
  not not_4 (not_4_out, not_2_out);
  not not_5 (not_5_out, not_4_out);
  CY7C199_SRAM cy7c199_sram_1 (
    .Output(controlled_buffer_1_out), .WEi(not_7_out), .CEi(Address[15]), .OEi(not_1_out),
    .Address(Address[14:0]), .Input(controlled_buffer_1_out));
  CY7C199_SRAM cy7c199_sram_2 (
    .Output(controlled_buffer_1_out), .WEi(not_7_out), .CEi(not_6_out), .OEi(not_1_out),
    .Address(Address[14:0]), .Input(controlled_buffer_1_out));
  not not_6 (not_6_out, Address[15]);
  and and_2 (and_2_out, Write, and_1_out);
  not not_7 (not_7_out, and_2_out);
endmodule

module RAMInterface_Keyboard (
  input  [15:0] MARIn,
  input  [7:0] DataBusIn,
  input  Manual,
  input  DataOut,
  input  WE,
  input  CLK,
  input  WriteValue,
  input  [7:0] RAMDataOut,
  input  DecAddress,
  input  IncAddress,
  input  OutValue,
  input  TYPE_ADDRESS,
  input  BUTTON_0,
  input  BUTTON_1,
  input  BUTTON_2,
  input  BUTTON_3,
  input  BUTTON_4,
  input  BUTTON_5,
  input  BUTTON_6,
  input  BUTTON_7,
  input  BUTTON_8,
  input  BUTTON_9,
  input  BUTTON_10,
  input  BUTTON_11,
  input  BUTTON_12,
  input  BUTTON_13,
  input  BUTTON_14,
  input  BUTTON_15,
  output [15:0] RAMAddress,
  output [7:0] RAMDataIn,
  output RAMOut,
  output A3,
  output RAMWrite,
  output B3,
  output RAMClk,
  output A4,
  output C3,
  output B4,
  output D3,
  output C4,
  output E3,
  output D4,
  output F3,
  output E4,
  output G3,
  output F4,
  output G4,
  output [7:0] DataBusOut,
  output A2,
  output B2,
  output A1,
  output C2,
  output B1,
  output D2,
  output C1,
  output E2,
  output D1,
  output F2,
  output E1,
  output G2,
  output F1,
  output G1
);

  wire and_1_out, hct193_updowncounter_1_tcdi, hct193_updowncounter_1_tcui, nand_1_out, nor_1_out, not_1_out,
       not_2_out, not_3_out, not_4_out, not_5_out, not_6_out, not_7_out, not_8_out, not_9_out, not_10_out,
       not_11_out, not_12_out, not_13_out, not_14_out, not_15_out, not_16_out, not_18_out, or_1_out;
  wire [2:2] not_17_out;
  wire [3:0] controlled_buffer_5_out;
  wire [7:0] hct193_updowncounter_1_q0, hct574_octallatch_1_q, or_5_out;

  not not_1 (not_1_out, Manual);
  not not_2 (not_2_out, DecAddress);
  nor nor_1 (nor_1_out, IncAddress, not_17_out[2]);
  assign RAMDataIn = not_1_out ? DataBusIn : 8'bz;  // Controlled_Buffer controlled_buffer_1
  assign RAMDataIn = Manual ? hct574_octallatch_1_q : 8'bz;  // Controlled_Buffer controlled_buffer_2
  HEXTo7SD hexto7sd_1 (.Display({A3, B3, C3, D3, E3, F3, G3}), .Value(hct193_updowncounter_1_q0[3:0]));
  HCT193_UpDownCounter hct193_updowncounter_1 (
    .Q0(hct193_updowncounter_1_q0[0]), .Q1(hct193_updowncounter_1_q0[1]), .Q2(hct193_updowncounter_1_q0[2]),
    .Q3(hct193_updowncounter_1_q0[3]), .TCDi(hct193_updowncounter_1_tcdi),
    .TCUi(hct193_updowncounter_1_tcui), .PLi(nand_1_out), .CPUi(nor_1_out), .P0(controlled_buffer_5_out[0]),
    .P1(controlled_buffer_5_out[1]), .P2(controlled_buffer_5_out[2]), .P3(controlled_buffer_5_out[3]),
    .CPDi(not_2_out), .MR(1'b0));
  nand nand_1 (nand_1_out, not_3_out, and_1_out);
  not not_3 (not_3_out, not_4_out);
  not not_4 (not_4_out, not_5_out);
  not not_5 (not_5_out, and_1_out);
  and and_1 (and_1_out, not_6_out, TYPE_ADDRESS);
  HEXTo7SD hexto7sd_2 (.Display({A4, B4, C4, D4, E4, F4, G4}), .Value(hct193_updowncounter_1_q0[7:4]));
  HCT193_UpDownCounter hct193_updowncounter_2 (
    .Q0(hct193_updowncounter_1_q0[4]), .Q1(hct193_updowncounter_1_q0[5]), .Q2(hct193_updowncounter_1_q0[6]),
    .Q3(hct193_updowncounter_1_q0[7]), .PLi(nand_1_out), .CPUi(hct193_updowncounter_1_tcui),
    .P0(hct193_updowncounter_1_q0[0]), .P1(hct193_updowncounter_1_q0[1]), .P2(hct193_updowncounter_1_q0[2]),
    .P3(hct193_updowncounter_1_q0[3]), .CPDi(hct193_updowncounter_1_tcdi), .MR(1'b0));  // open: TCDi, TCUi
  not not_6 (not_6_out, not_7_out);
  not not_7 (not_7_out, not_8_out);
  not not_8 (not_8_out, not_9_out);
  not not_9 (not_9_out, not_10_out);
  not not_10 (not_10_out, not_11_out);
  not not_11 (not_11_out, or_1_out);
  or or_1 (or_1_out, BUTTON_0, BUTTON_1, BUTTON_2, BUTTON_3, BUTTON_4, BUTTON_5, BUTTON_6, BUTTON_7, BUTTON_8, BUTTON_9, BUTTON_10, BUTTON_11, BUTTON_12, BUTTON_13, BUTTON_14, BUTTON_15);
  not not_12 (not_12_out, Manual);
  assign RAMAddress = not_12_out ? MARIn : 16'bz;  // Controlled_Buffer controlled_buffer_3
  assign RAMAddress = Manual ? {{8{1'b0}}, hct193_updowncounter_1_q0} : 16'bz;  // Controlled_Buffer controlled_buffer_4
  not not_13 (not_13_out, WriteValue);
  not not_14 (not_14_out, OutValue);
  assign {controlled_buffer_5_out, or_5_out[7:4]} = not_14_out ? hct574_octallatch_1_q : 8'bz;  // Controlled_Buffer controlled_buffer_5
  assign {controlled_buffer_5_out, or_5_out[7:4]} = OutValue ? RAMDataOut : 8'bz;  // Controlled_Buffer controlled_buffer_6
  HCT574_OctalLatch hct574_octallatch_1 (.Q(hct574_octallatch_1_q), .CP(not_6_out), .D(or_5_out), .OEi(1'b0));
  or or_2 (or_5_out[3], BUTTON_8, BUTTON_9, BUTTON_10, BUTTON_11, BUTTON_12, BUTTON_13, BUTTON_14, BUTTON_15);
  not not_15 (not_15_out, not_13_out);
  not not_16 (not_16_out, not_15_out);
  not not_17 (not_17_out[2], not_16_out);
  or or_3 (or_5_out[2], BUTTON_4, BUTTON_5, BUTTON_6, BUTTON_7, BUTTON_12, BUTTON_13, BUTTON_14, BUTTON_15);
  assign {RAMClk, RAMWrite, RAMOut} = not_18_out ? {CLK, WE, DataOut} : 3'bz;  // Controlled_Buffer controlled_buffer_7
  not not_18 (not_18_out, Manual);
  assign {RAMClk, RAMWrite, RAMOut} = Manual ? {not_17_out[2], WriteValue, OutValue} : 3'bz;  // Controlled_Buffer controlled_buffer_8
  HEXTo7SD hexto7sd_3 (.Display({A2, B2, C2, D2, E2, F2, G2}), .Value(controlled_buffer_5_out));
  or or_4 (or_5_out[1], BUTTON_2, BUTTON_3, BUTTON_6, BUTTON_7, BUTTON_10, BUTTON_11, BUTTON_14, BUTTON_15);
  HEXTo7SD hexto7sd_4 (.Display({A1, B1, C1, D1, E1, F1, G1}), .Value(or_5_out[7:4]));
  or or_5 (or_5_out[0], BUTTON_1, BUTTON_3, BUTTON_5, BUTTON_7, BUTTON_9, BUTTON_11, BUTTON_13, BUTTON_15);

  assign DataBusOut = RAMDataOut;

  // Notes on the sheet:
  //   Lower
  //   Address
  //   Will need to use more than 1 buffer for address line
  //   Upper
  //   Run these through octal buffer
  //   Delay write signal for manual clock
  //   Upper
  //   Data
  //   Lower
endmodule

module MARFirstModule (
  input  [7:0] AddressBusIn,
  input  [7:0] AddressIn,
  input  [7:0] IDIn,
  input  ADD,
  input  Reset,
  input  Clk,
  input  In8,
  input  Inc,
  input  LoadFull,
  input  ZSIn,
  input  OutI,
  input  [7:0] Out8In,
  output [7:0] IDOut,
  output ResetOut,
  output [7:0] AddressOut,
  output In8O,
  output ClkOut,
  output RC,
  output LoadFullO,
  output ZSOut,
  output [7:0] Value,
  output OutO,
  output [7:0] Out8Out
);

  wire and_1_out, and_2_out, and_3_out, and_4_out, and_6_out, hct193_updowncounter_1_tcdi,
       hct193_updowncounter_1_tcui, hct193_updowncounter_2_tcui, hct283_adder_1_cout, hct283_adder_2_cout,
       nand_1_out, nor_1_out, nor_2_out, not_1_out, not_2_out, not_3_out, not_4_out, not_5_out;
  wire [3:0] hct157_selctormultiplexer_1_y, hct157_selctormultiplexer_2_y, hct193_updowncounter_1_q0,
       hct193_updowncounter_2_q0, hct283_adder_1_s, hct283_adder_2_s;

  not not_1 (not_1_out, Clk);
  and and_1 (and_1_out, Clk, not_3_out);
  not not_2 (not_2_out, not_1_out);
  not not_3 (not_3_out, not_2_out);
  and and_2 (and_2_out, IDIn[0], and_1_out);
  and and_3 (and_3_out, and_1_out, LoadFull);
  and and_4 (and_4_out, and_2_out, In8);
  nand nand_1 (nand_1_out, Clk, Inc);
  and and_5 (ZSOut, nor_2_out, ZSIn);
  HCT283_Adder hct283_adder_1 (
    .CIn(1'b0), .A(AddressIn[3:0]), .B(hct193_updowncounter_1_q0), .S(hct283_adder_1_s),
    .COut(hct283_adder_1_cout));
  HCT283_Adder hct283_adder_2 (
    .CIn(hct283_adder_1_cout), .A(AddressIn[7:4]), .B(hct193_updowncounter_2_q0), .S(hct283_adder_2_s),
    .COut(hct283_adder_2_cout));
  and and_6 (and_6_out, hct283_adder_2_cout, ADD);
  nor nor_1 (nor_1_out, and_3_out, and_4_out);
  nor nor_2 (nor_2_out, hct193_updowncounter_1_q0[0], hct193_updowncounter_1_q0[1], hct193_updowncounter_1_q0[2], hct193_updowncounter_1_q0[3], hct193_updowncounter_2_q0[1], hct193_updowncounter_2_q0[2], hct193_updowncounter_2_q0[3], hct193_updowncounter_2_q0[0]);
  Pull_Resistor #(.pull(1)) pull_resistor_1 (.node(ZSIn));
  HCT157_SelctorMultiplexer hct157_selctormultiplexer_1 (
    .Y(hct157_selctormultiplexer_1_y), .A(AddressIn[3:0]), .B(hct283_adder_1_s), .S(ADD), .Ei(1'b0));
  HCT157_SelctorMultiplexer hct157_selctormultiplexer_2 (
    .Y(hct157_selctormultiplexer_2_y), .A(AddressIn[7:4]), .B(hct283_adder_2_s), .S(ADD), .Ei(1'b0));
  HCT193_UpDownCounter hct193_updowncounter_1 (
    .Q0(hct193_updowncounter_1_q0[0]), .Q1(hct193_updowncounter_1_q0[1]), .Q2(hct193_updowncounter_1_q0[2]),
    .Q3(hct193_updowncounter_1_q0[3]), .TCDi(hct193_updowncounter_1_tcdi),
    .TCUi(hct193_updowncounter_1_tcui), .PLi(nor_1_out), .CPUi(nand_1_out), .P0(AddressOut[0]),
    .P1(AddressOut[1]), .P2(AddressOut[2]), .P3(AddressOut[3]), .CPDi(1'b1), .MR(Reset));
  assign Out8Out = IDIn[0] ? {hct193_updowncounter_2_q0, hct193_updowncounter_1_q0} : 8'bz;  // Controlled_Buffer controlled_buffer_1
  assign Out8Out = not_5_out ? Out8In : 8'bz;  // Controlled_Buffer controlled_buffer_2
  HCT157_SelctorMultiplexer hct157_selctormultiplexer_3 (
    .Y(AddressOut[3:0]), .A(hct157_selctormultiplexer_1_y), .B(AddressBusIn[3:0]), .S(LoadFull), .Ei(1'b0));
  HCT157_SelctorMultiplexer hct157_selctormultiplexer_4 (
    .Y(AddressOut[7:4]), .A(hct157_selctormultiplexer_2_y), .B(AddressBusIn[7:4]), .S(LoadFull), .Ei(1'b0));
  HCT193_UpDownCounter hct193_updowncounter_2 (
    .Q0(hct193_updowncounter_2_q0[0]), .Q1(hct193_updowncounter_2_q0[1]), .Q2(hct193_updowncounter_2_q0[2]),
    .Q3(hct193_updowncounter_2_q0[3]), .TCUi(hct193_updowncounter_2_tcui), .PLi(nor_1_out),
    .CPUi(hct193_updowncounter_1_tcui), .P0(AddressOut[4]), .P1(AddressOut[5]), .P2(AddressOut[6]),
    .P3(AddressOut[7]), .CPDi(hct193_updowncounter_1_tcdi), .MR(Reset));  // open: TCDi
  not not_4 (not_4_out, hct193_updowncounter_2_tcui);
  DotMatrix #(.matrixcols(8), .matrixrows(1)) dotmatrix_1 (
    .col0(hct193_updowncounter_2_q0[3]), .col1(hct193_updowncounter_2_q0[2]),
    .col2(hct193_updowncounter_2_q0[1]), .col3(hct193_updowncounter_2_q0[0]),
    .col4(hct193_updowncounter_1_q0[3]), .col5(hct193_updowncounter_1_q0[2]),
    .col6(hct193_updowncounter_1_q0[1]), .col7(hct193_updowncounter_1_q0[0]));
  assign Value = OutI ? {hct193_updowncounter_2_q0, hct193_updowncounter_1_q0} : 8'bz;  // Controlled_Buffer controlled_buffer_3
  not not_5 (not_5_out, IDIn[0]);
  or or_1 (RC, and_6_out, not_4_out);

  assign ClkOut = Clk;
  assign IDOut = {IDIn[0], IDIn[7:1]};
  assign In8O = In8;
  assign LoadFullO = LoadFull;
  assign OutO = OutI;
  assign ResetOut = Reset;

  // Notes on the sheet:
  //   ZSIn: pull=up
  //   Enable Line
  //   Logisim
endmodule

module Address_Module (
  input  [7:0] AddressIn,
  input  [7:0] AddressBusIn,
  input  [7:0] IDIn,
  input  Reset,
  input  Clk,
  input  In8,
  input  Inc,
  input  LoadFull,
  input  ZSIn,
  input  OutI,
  input  [7:0] Out8In,
  output [7:0] IDOut,
  output ResetOut,
  output [7:0] AddressOut,
  output In8O,
  output ClkOut,
  output RC,
  output LoadFullO,
  output ZSOut,
  output [7:0] Value,
  output OutO,
  output [7:0] Out8Out
);

  wire and_1_out, and_2_out, and_3_out, and_4_out, hct193_updowncounter_1_tcdi, hct193_updowncounter_1_tcui,
       hct193_updowncounter_2_tcui, nand_1_out, nor_1_out, nor_2_out, not_1_out, not_2_out, not_3_out,
       not_5_out;
  wire [7:0] hct193_updowncounter_1_q0;

  not not_1 (not_1_out, Clk);
  and and_1 (and_1_out, Clk, not_3_out);
  not not_2 (not_2_out, not_1_out);
  not not_3 (not_3_out, not_2_out);
  and and_2 (and_2_out, IDIn[0], and_1_out);
  and and_3 (and_3_out, and_1_out, LoadFull);
  and and_4 (and_4_out, and_2_out, In8);
  nand nand_1 (nand_1_out, Clk, Inc);
  and and_5 (ZSOut, nor_2_out, ZSIn);
  HCT157_SelctorMultiplexer hct157_selctormultiplexer_1 (
    .Y(AddressOut[3:0]), .A(AddressIn[3:0]), .B(AddressBusIn[3:0]), .S(LoadFull), .Ei(1'b0));
  HCT157_SelctorMultiplexer hct157_selctormultiplexer_2 (
    .Y(AddressOut[7:4]), .A(AddressIn[7:4]), .B(AddressBusIn[7:4]), .S(LoadFull), .Ei(1'b0));
  nor nor_1 (nor_1_out, and_3_out, and_4_out);
  nor nor_2 (nor_2_out, hct193_updowncounter_1_q0[0], hct193_updowncounter_1_q0[1], hct193_updowncounter_1_q0[2], hct193_updowncounter_1_q0[3], hct193_updowncounter_1_q0[5], hct193_updowncounter_1_q0[6], hct193_updowncounter_1_q0[7], hct193_updowncounter_1_q0[4]);
  Pull_Resistor #(.pull(1)) pull_resistor_1 (.node(ZSIn));
  HCT193_UpDownCounter hct193_updowncounter_1 (
    .Q0(hct193_updowncounter_1_q0[0]), .Q1(hct193_updowncounter_1_q0[1]), .Q2(hct193_updowncounter_1_q0[2]),
    .Q3(hct193_updowncounter_1_q0[3]), .TCDi(hct193_updowncounter_1_tcdi),
    .TCUi(hct193_updowncounter_1_tcui), .PLi(nor_1_out), .CPUi(nand_1_out), .P0(AddressOut[0]),
    .P1(AddressOut[1]), .P2(AddressOut[2]), .P3(AddressOut[3]), .CPDi(1'b1), .MR(Reset));
  assign Out8Out = IDIn[0] ? hct193_updowncounter_1_q0 : 8'bz;  // Controlled_Buffer controlled_buffer_1
  assign Out8Out = not_5_out ? Out8In : 8'bz;  // Controlled_Buffer controlled_buffer_2
  HCT193_UpDownCounter hct193_updowncounter_2 (
    .Q0(hct193_updowncounter_1_q0[4]), .Q1(hct193_updowncounter_1_q0[5]), .Q2(hct193_updowncounter_1_q0[6]),
    .Q3(hct193_updowncounter_1_q0[7]), .TCUi(hct193_updowncounter_2_tcui), .PLi(nor_1_out),
    .CPUi(hct193_updowncounter_1_tcui), .P0(AddressOut[4]), .P1(AddressOut[5]), .P2(AddressOut[6]),
    .P3(AddressOut[7]), .CPDi(hct193_updowncounter_1_tcdi), .MR(Reset));  // open: TCDi
  not not_4 (RC, hct193_updowncounter_2_tcui);
  DotMatrix #(.matrixcols(8), .matrixrows(1)) dotmatrix_1 (
    .col0(hct193_updowncounter_1_q0[7]), .col1(hct193_updowncounter_1_q0[6]),
    .col2(hct193_updowncounter_1_q0[5]), .col3(hct193_updowncounter_1_q0[4]),
    .col4(hct193_updowncounter_1_q0[3]), .col5(hct193_updowncounter_1_q0[2]),
    .col6(hct193_updowncounter_1_q0[1]), .col7(hct193_updowncounter_1_q0[0]));
  assign Value = OutI ? hct193_updowncounter_1_q0 : 8'bz;  // Controlled_Buffer controlled_buffer_3
  not not_5 (not_5_out, IDIn[0]);

  assign ClkOut = Clk;
  assign IDOut = {IDIn[0], IDIn[7:1]};
  assign In8O = In8;
  assign LoadFullO = LoadFull;
  assign OutO = OutI;
  assign ResetOut = Reset;

  // Notes on the sheet:
  //   ZSIn: pull=up
  //   Enable Line
  //   Logisim
endmodule

module Address_Controller (
  input  [7:0] IDIn,
  input  Clk,
  input  [8:0] RegisterOps,
  input  [7:0] Data8In,
  input  EnableRegister,
  input  MasterReset,
  input  RegOut,
  output [7:0] IDOut,
  output IndexEnd,
  output ClkO,
  output [7:0] Data8Out,
  output Load8,
  output FullLoad,
  output Inc,
  output Reset,
  output Add,
  output DataOut
);

  wire and_1_out, and_2_out, and_3_out, and_4_out, and_8_out, and_10_out, not_1_out, not_2_out, not_3_out,
       not_4_out, or_1_out, or_2_out, or_3_out;
  wire [7:0] controlled_buffer_2_out;

  not not_1 (not_1_out, not_2_out);
  not not_2 (not_2_out, not_3_out);
  or or_1 (or_1_out, RegisterOps[1], not_1_out);
  not not_3 (not_3_out, not_4_out);
  not not_4 (not_4_out, Load8);
  and and_1 (and_1_out, EnableRegister, RegisterOps[0]);
  or or_2 (or_2_out, and_1_out, and_2_out);
  and and_2 (and_2_out, or_1_out, EnableRegister);
  and and_3 (and_3_out, EnableRegister, RegisterOps[2]);
  and and_4 (and_4_out, EnableRegister, RegisterOps[3]);
  assign Data8Out = and_4_out ? Data8In : 8'bz;  // Controlled_Buffer controlled_buffer_1
  and and_5 (Load8, EnableRegister, RegisterOps[4]);
  and and_6 (FullLoad, RegisterOps[5], EnableRegister);
  and and_7 (Inc, RegisterOps[6], EnableRegister);
  and and_8 (and_8_out, RegisterOps[7], EnableRegister);
  and and_9 (Add, RegisterOps[8], EnableRegister);
  assign {controlled_buffer_2_out[6:0], controlled_buffer_2_out[7]} = and_2_out ? IDOut : 8'bz;  // Controlled_Buffer controlled_buffer_2
  assign controlled_buffer_2_out = and_3_out ? IDIn : 8'bz;  // Controlled_Buffer controlled_buffer_3
  or or_3 (or_3_out, or_2_out, and_3_out);
  and and_10 (and_10_out, or_3_out, Clk);
  assign {controlled_buffer_2_out[0], controlled_buffer_2_out[7:1]} = and_1_out ? IDOut : 8'bz;  // Controlled_Buffer controlled_buffer_4
  HCT574_OctalLatch hct574_octallatch_1 (.Q(IDOut), .CP(and_10_out), .D(controlled_buffer_2_out), .OEi(1'b0));
  or or_4 (Reset, and_8_out, MasterReset);

  assign ClkO = Clk;
  assign DataOut = RegOut;
  assign IndexEnd = IDOut[7];

  // Notes on the sheet:
  //   Output8Bits
  //   IncID
  //   DecID
  //   LoadID
endmodule

module Register_Module (
  input  [7:0] Data,
  input  Load,
  input  Reset,
  input  Dec,
  input  Carry,
  input  Inc,
  input  Clk,
  input  Enablei,
  input  BypassOuti,
  input  OE,
  input  LHSE,
  input  RHSE,
  output CarryOut,
  output BorrowOut,
  output [7:0] DataOut,
  output [7:0] LHO,
  output [7:0] RHO
);

  wire and_1_out, and_2_out, and_3_out, and_4_out, and_5_out, button_1_out, ClkEdge, d_ff_1_qn, d_ff_2_qn,
       hct193_updowncounter_1_tcdi, hct193_updowncounter_1_tcui, hct193_updowncounter_2_tcdi,
       hct193_updowncounter_2_tcui, nand_1_out, nand_2_out, nand_3_out, nand_4_out, nand_5_out, not_1_out,
       not_2_out, not_3_out, not_4_out, not_5_out, not_6_out, not_7_out, not_8_out, or_2_out;
  wire [7:0] hct193_updowncounter_1_q0;

  not not_1 (not_1_out, Enablei);
  and and_1 (and_1_out, not_1_out, Load);
  and and_2 (and_2_out, Dec, Carry);
  and and_3 (and_3_out, Carry, Inc);
  and and_4 (and_4_out, Clk, not_1_out);
  nand nand_1 (nand_1_out, OE, not_1_out);
  not not_2 (not_2_out, LHSE);
  not not_3 (not_3_out, RHSE);
  not not_4 (not_4_out, and_4_out);
  not not_5 (not_5_out, not_4_out);
  not not_6 (not_6_out, not_5_out);
  Button button_1 (.out(button_1_out));
  nand nand_2 (nand_2_out, and_2_out, and_4_out);
  nand nand_3 (nand_3_out, and_3_out, and_4_out);
  nand nand_4 (nand_4_out, BypassOuti, nand_1_out);
  nand nand_5 (nand_5_out, and_1_out, and_5_out);
  and and_5 (and_5_out, and_4_out, not_6_out);
  or or_1 (ClkEdge, and_4_out, not_6_out);
  or or_2 (or_2_out, Reset, button_1_out);
  HCT193_UpDownCounter hct193_updowncounter_1 (
    .Q0(hct193_updowncounter_1_q0[0]), .Q1(hct193_updowncounter_1_q0[1]), .Q2(hct193_updowncounter_1_q0[2]),
    .Q3(hct193_updowncounter_1_q0[3]), .TCDi(hct193_updowncounter_1_tcdi),
    .TCUi(hct193_updowncounter_1_tcui), .PLi(nand_5_out), .CPUi(nand_3_out), .P0(Data[0]), .P1(Data[1]),
    .P2(Data[2]), .P3(Data[3]), .CPDi(nand_2_out), .MR(or_2_out));
  HCT193_UpDownCounter hct193_updowncounter_2 (
    .Q0(hct193_updowncounter_1_q0[4]), .Q1(hct193_updowncounter_1_q0[5]), .Q2(hct193_updowncounter_1_q0[6]),
    .Q3(hct193_updowncounter_1_q0[7]), .TCDi(hct193_updowncounter_2_tcdi),
    .TCUi(hct193_updowncounter_2_tcui), .PLi(nand_5_out), .CPUi(hct193_updowncounter_1_tcui), .P0(Data[4]),
    .P1(Data[5]), .P2(Data[6]), .P3(Data[7]), .CPDi(hct193_updowncounter_1_tcdi), .MR(or_2_out));
  assign DataOut = nand_4_out ? hct193_updowncounter_1_q0 : 8'bz;  // Controlled_Buffer controlled_buffer_1
  assign LHO = not_2_out ? hct193_updowncounter_1_q0 : 8'bz;  // Controlled_Buffer controlled_buffer_2
  assign RHO = not_3_out ? hct193_updowncounter_1_q0 : 8'bz;  // Controlled_Buffer controlled_buffer_3
  D_Flip_Flop d_ff_1 (
    .D(hct193_updowncounter_2_tcui), .clk(ClkEdge), .Qn(d_ff_1_qn), .preset(1'b0), .reset(1'b0));  // open: Q
  D_Flip_Flop d_ff_2 (
    .D(hct193_updowncounter_2_tcdi), .clk(ClkEdge), .Qn(d_ff_2_qn), .preset(1'b0), .reset(1'b0));  // open: Q
  Transistor #(.gate("br")) transistor_1 (.in(1'b1), .out(CarryOut), .gate(not_7_out));
  not not_7 (not_7_out, d_ff_1_qn);
  not not_8 (not_8_out, d_ff_2_qn);
  Transistor transistor_2 (.in(1'b1), .out(BorrowOut), .gate(not_8_out));

  // Notes on the sheet:
  //   Bus In
  //   Main Bus Out
  //   ALU Buses Out
  //   N-Type, not P. BOX for Logisim ONLY
  //   Chip Count
  //   2 HCT 193
  //   3 HCT245
  //   2 OR -- 1 Chips
  //   4 AND -- 1 Chips
  //   6 NOT -- 1 Chips
  //   16 NAND -- 4 Chip
  //   3 Transistors
endmodule

module Register_Controller (
  input  BypassedOuti,
  input  [7:0] DataBus,
  input  CLK,
  input  RControllerIn,
  input  Crement,
  input  RIn,
  input  CarryIn,
  input  RReset,
  input  ROut,
  input  RegisterCarry,
  input  RegisterBorrow,
  input  [7:0] RegisterBusOut,
  output Enable0i,
  output Enable1i,
  output [7:0] DataBusIn,
  output Output0i,
  output Enable2i,
  output Output1i,
  output Enable3i,
  output Output2i,
  output CLKOut,
  output Output3i,
  output RHO0i,
  output Inc,
  output RHO1i,
  output Dec,
  output RHO2i,
  output CarryToReg,
  output RHO3i,
  output Load,
  output LHO0i,
  output Reset,
  output LHO1i,
  output OE,
  output LHO2i,
  output LHO3i,
  output CarryResult,
  output BorrowResult,
  output [7:0] DataBusOut
);

  wire and_1_out, and_2_out, nand_1_out, not_1_out, not_2_out, not_3_out, not_4_out, not_5_out, not_6_out,
       or_1_out;
  wire [7:0] hct574_octallatch_1_q;

  not not_1 (not_1_out, CLK);
  not not_2 (not_2_out, not_1_out);
  not not_3 (not_3_out, not_2_out);
  HCT574_OctalLatch hct574_octallatch_1 (.Q(hct574_octallatch_1_q), .CP(and_2_out), .D(DataBus), .OEi(1'b0));
  and and_1 (and_1_out, CLK, not_3_out);
  and and_2 (and_2_out, and_1_out, RControllerIn);
  and and_3 (CarryResult, RegisterCarry, hct574_octallatch_1_q[2]);
  and and_4 (BorrowResult, hct574_octallatch_1_q[2], RegisterBorrow);
  and and_5 (Inc, hct574_octallatch_1_q[3], Crement);
  not not_4 (not_4_out, hct574_octallatch_1_q[3]);
  and and_6 (Dec, Crement, not_4_out);
  nand nand_1 (nand_1_out, hct574_octallatch_1_q[2], not_5_out);
  not not_5 (not_5_out, CarryIn);
  not not_6 (not_6_out, BypassedOuti);
  or or_1 (or_1_out, ROut, not_6_out);
  assign DataBusOut = or_1_out ? RegisterBusOut : 8'bz;  // Controlled_Buffer controlled_buffer_1
  and and_7 (CarryToReg, Crement, nand_1_out);
  HCT139_2to4LineDecoder hct139_2to4linedecoder_1 (
    .Y12(Output2i), .Y13(Output3i), .Y20(Enable0i), .Y21(Enable1i), .Y22(Enable2i), .Y23(Enable3i),
    .Y10(Output0i), .Y11(Output1i), .B1(hct574_octallatch_1_q[3]), .G2i(1'b0), .A2(hct574_octallatch_1_q[0]),
    .B2(hct574_octallatch_1_q[1]), .G1i(BypassedOuti), .A1(hct574_octallatch_1_q[2]));
  HCT139_2to4LineDecoder hct139_2to4linedecoder_2 (
    .Y12(LHO2i), .Y13(LHO3i), .Y20(RHO0i), .Y21(RHO1i), .Y22(RHO2i), .Y23(RHO3i), .Y10(LHO0i), .Y11(LHO1i),
    .B1(hct574_octallatch_1_q[5]), .G2i(1'b0), .A2(hct574_octallatch_1_q[2]), .B2(hct574_octallatch_1_q[3]),
    .G1i(1'b0), .A1(hct574_octallatch_1_q[4]));

  assign CLKOut = CLK;
  assign DataBusIn = DataBus;
  assign Load = RIn;
  assign OE = ROut;
  assign Reset = RReset;

  // Other names for the same wires on the sheet: BPOi = BypassedOuti; RO = ROut

  // Notes on the sheet:
  //   Logisim
  //   Chip Counts
  //   2 74HCT139
  //   1 74HCT574
  //   8 AND -- 2 Chips
  //   6 NOT -- 1 Chips
endmodule

module ALU (
  input  CarryIn,
  input  [7:0] LeftHandIn,
  input  EO,
  input  [7:0] RightHandIn,
  input  [7:0] Instruction,
  input  InstrIn,
  input  CLK,
  input  Carry,
  input  ShiftLeft,
  input  ShiftRight,
  input  RotL,
  input  RotR,
  input  ClockLine,
  input  EnableLine,
  output [7:0] DataOut,
  output CarryOut,
  output BorrowOut,
  output out_18,
  output out_19
);

  wire and_1_out, and_2_out, and_3_out, and_5_out, and_6_out, and_7_out, and_8_out, and_10_out, and_11_out,
       and_12_out, and_13_out, and_14_out, and_15_out, hc153_4to1multiplexer_1_y1,
       hc153_4to1multiplexer_1_y2, hct283_adder_1_cout, nand_1_out, nand_2_out, nand_3_out, nand_4_out,
       nor_1_out, nor_2_out, nor_3_out, not_1_out, not_2_out, not_3_out, not_4_out, not_5_out, not_6_out,
       not_7_out, not_8_out, not_9_out, not_10_out, not_11_out, not_12_out, not_13_out, not_14_out,
       not_15_out, not_16_out, or_2_out, or_3_out, or_4_out, or_5_out, or_6_out, s_r_ff_1_q, s_r_ff_2_q,
       transistor_1_out, transistor_2_out, undriven, xor_3_out;
  wire [1:0] controlled_buffer_7_out;
  wire [3:0] hct283_adder_1_s, hct283_adder_2_s;
  wire [7:0] and_4_out, controlled_buffer_1_out, controlled_buffer_4_out, controlled_buffer_7_out_2,
       hct574_octallatch_1_q, or_1_out, undriven_2, xor_1_out, xor_2_out;

  and and_1 (and_1_out, InstrIn, CLK);
  not not_1 (not_1_out, and_1_out);
  not not_2 (not_2_out, not_1_out);
  not not_3 (not_3_out, not_2_out);
  HCT574_OctalLatch hct574_octallatch_1 (.Q(hct574_octallatch_1_q), .CP(and_2_out), .D(Instruction), .OEi(1'b0));
  and and_2 (and_2_out, and_1_out, not_3_out);
  not not_4 (not_4_out, hct574_octallatch_1_q[2]);
  and and_3 (and_3_out, hct574_octallatch_1_q[1], not_4_out);
  nor nor_1 (nor_1_out, hct574_octallatch_1_q[2], hct574_octallatch_1_q[1]);
  assign and_4_out = LeftHandIn & RightHandIn;  // AND_Gate and_4, 8 bits wide
  assign controlled_buffer_1_out = nor_1_out ? and_4_out : 8'bz;  // Controlled_Buffer controlled_buffer_1
  assign or_1_out = LeftHandIn | RightHandIn;  // OR_Gate or_1, 8 bits wide
  assign xor_1_out = LeftHandIn ^ RightHandIn;  // XOR_Gate xor_1, 8 bits wide
  and and_5 (and_5_out, CarryIn, hct574_octallatch_1_q[0]);
  assign xor_2_out = RightHandIn ^ {8{hct574_octallatch_1_q[1]}};  // XOR_Gate xor_2, 8 bits wide
  not not_5 (not_5_out, hct574_octallatch_1_q[1]);
  and and_6 (and_6_out, hct574_octallatch_1_q[2], not_5_out);
  assign controlled_buffer_1_out = and_3_out ? or_1_out : 8'bz;  // Controlled_Buffer controlled_buffer_2
  assign controlled_buffer_1_out = and_6_out ? xor_1_out : 8'bz;  // Controlled_Buffer controlled_buffer_3
  xor xor_3 (xor_3_out, and_5_out, hct574_octallatch_1_q[1]);
  HCT283_Adder hct283_adder_1 (
    .CIn(xor_3_out), .A(LeftHandIn[3:0]), .B(xor_2_out[3:0]), .S(hct283_adder_1_s), .COut(hct283_adder_1_cout));
  HCT283_Adder hct283_adder_2 (
    .CIn(hct283_adder_1_cout), .A(LeftHandIn[7:4]), .B(xor_2_out[7:4]), .S(hct283_adder_2_s), .COut(CarryOut));
  assign controlled_buffer_4_out = and_7_out ? controlled_buffer_1_out : 8'bz;  // Controlled_Buffer controlled_buffer_4
  and and_7 (and_7_out, hct574_octallatch_1_q[3], hct574_octallatch_1_q[6]);
  and and_8 (and_8_out, hct574_octallatch_1_q[6], not_6_out);
  not not_6 (not_6_out, hct574_octallatch_1_q[3]);
  assign controlled_buffer_4_out = and_8_out ? {hct283_adder_2_s, hct283_adder_1_s} : 8'bz;  // Controlled_Buffer controlled_buffer_5
  not not_7 (not_7_out, nor_2_out);
  or or_2 (or_2_out, not_7_out, or_3_out);
  or or_3 (or_3_out, ShiftLeft, ShiftRight);
  assign DataOut = EO ? controlled_buffer_4_out : 8'bz;  // Controlled_Buffer controlled_buffer_6
  and and_9 (BorrowOut, controlled_buffer_4_out[7], hct574_octallatch_1_q[1]);
  Transistor transistor_1 (.in(hc153_4to1multiplexer_1_y2), .out(transistor_1_out), .gate(undriven));
  Transistor #(.gate("br")) transistor_2 (.in(hc153_4to1multiplexer_1_y1), .out(transistor_2_out), .gate(undriven));
  or or_4 (or_4_out, ShiftLeft, RotL);
  nor nor_2 (nor_2_out, RotL, RotR);
  and and_10 (and_10_out, ShiftLeft, undriven_2[7]);
  or or_5 (or_5_out, or_2_out, ClockLine);
  not not_8 (not_8_out, or_5_out);
  not not_9 (not_9_out, not_8_out);
  not not_10 (not_10_out, not_9_out);
  HC153_4To1MultiPlexer hc153_4to1multiplexer_1 (
    .Y1(hc153_4to1multiplexer_1_y1), .Y2(hc153_4to1multiplexer_1_y2), .D12(Carry),
    .D11(controlled_buffer_7_out_2[6]), .D10(controlled_buffer_7_out[0]), .S0(or_4_out), .S1(nor_2_out),
    .D23(Carry), .D22(controlled_buffer_7_out[1]), .D21(controlled_buffer_7_out_2[7]), .E1i(undriven),
    .D20(controlled_buffer_7_out[1]), .E2i(undriven), .D13(controlled_buffer_7_out_2[6]));
  and and_11 (and_11_out, ShiftRight, undriven_2[0]);
  and and_12 (and_12_out, or_5_out, not_10_out);
  and and_13 (and_13_out, ~undriven, or_6_out);  // AND_Gate
  or or_6 (or_6_out, ShiftLeft, RotL);
  assign {controlled_buffer_7_out_2[5:0], controlled_buffer_7_out} = nor_3_out ? undriven_2 : 8'bz;  // Controlled_Buffer controlled_buffer_7
  nor nor_3 (nor_3_out, or_6_out, undriven);
  not not_11 (not_11_out, nand_1_out);
  nand nand_1 (nand_1_out, and_10_out, and_12_out);
  S_R_Flip_Flop s_r_ff_1 (.Q(s_r_ff_1_q), .reset(not_12_out), .preset(not_11_out));  // open: S, R, clk, Qn
  not not_12 (not_12_out, nand_2_out);
  nand nand_2 (nand_2_out, nand_1_out, and_12_out);
  not not_13 (not_13_out, nand_3_out);
  nand nand_3 (nand_3_out, and_11_out, and_12_out);
  S_R_Flip_Flop s_r_ff_2 (.Q(s_r_ff_2_q), .reset(not_14_out), .preset(not_13_out));  // open: S, R, clk, Qn
  not not_14 (not_14_out, nand_4_out);
  nand nand_4 (nand_4_out, nand_3_out, and_12_out);
  assign controlled_buffer_7_out_2 = and_13_out ? undriven_2 : 8'bz;  // Controlled_Buffer controlled_buffer_8
  and and_14 (and_14_out, s_r_ff_1_q, EnableLine);
  and and_15 (and_15_out, EnableLine, s_r_ff_2_q);
  Transistor #(.gate("br")) transistor_3 (.in(1'b1), .out(out_18), .gate(not_15_out));
  not not_15 (not_15_out, and_15_out);
  not not_16 (not_16_out, and_14_out);
  Transistor transistor_4 (.in(1'b1), .out(out_19), .gate(not_16_out));

  // Notes on the sheet:
  //   Only 4 bits used
  //   Right Ops
  //   IGNORE NOTs
  //   Use 2 NANDs for SR Latch
  //   Left Ops
  //   N-Type, not P. BOX for Logisim ONLY
endmodule

module Instruction_Controller (
  input  [43:0] Decoded_Instruction,
  input  [43:0] Control_Line_Expansion,
  input  ExpansionControl,
  input  [7:0] DataBus,
  input  CLK,
  input  Reset,
  input  ESC,
  output HLT,
  output [7:0] Instruction,
  output [7:0] DataOut,
  output RCI,
  output RI,
  output RO,
  output RUC,
  output CRM,
  output BRO,
  output IID,
  output [3:0] StepOut,
  output DID,
  output IDI,
  output OUT8,
  output IN8,
  output FLOD,
  output IR,
  output ADR,
  output RSR,
  output MAR,
  output PC,
  output PCO,
  output GR,
  output GRO,
  output RMO,
  output RMI,
  output FSI,
  output SF,
  output CF,
  output LF,
  output FO,
  output DFI,
  output EO,
  output EII,
  output PSH,
  output POP,
  output IOI,
  output IOO,
  output IDO,
  output SID
);

  wire and_1_out, and_2_out, and_3_out, and_4_out, and_5_out, d_ff_1_q, d_ff_1_qn, nand_1_out, not_1_out,
       not_2_out, not_3_out, not_4_out, not_5_out, not_6_out, or_1_out, or_2_out, undriven;
  wire [43:0] or_3_out, pull_resistor_1_node, pull_resistor_2_node;
  wire [43:14] controlled_buffer_4_out;

  not not_1 (not_1_out, CLK);
  and and_1 (and_1_out, CLK, or_1_out);
  or or_1 (or_1_out, controlled_buffer_4_out[42], ESC);
  HCT574_OctalLatch hct574_octallatch_1 (.Q(Instruction), .CP(and_2_out), .D(DataBus), .OEi(1'b0));
  and and_2 (and_2_out, controlled_buffer_4_out[16], and_3_out);
  and and_3 (and_3_out, CLK, not_3_out);
  not not_2 (not_2_out, not_1_out);
  not not_3 (not_3_out, not_2_out);
  HCT193_UpDownCounter hct193_updowncounter_1 (
    .Q0(StepOut[0]), .Q1(StepOut[1]), .Q2(StepOut[2]), .Q3(StepOut[3]), .PLi(1'b1), .CPUi(not_4_out),
    .P0(1'b0), .P1(1'b0), .P2(1'b0), .P3(1'b0), .CPDi(1'b1), .MR(or_2_out));  // open: TCDi, TCUi
  not not_4 (not_4_out, and_1_out);
  not not_5 (not_5_out, or_1_out);
  D_Flip_Flop d_ff_1 (.D(d_ff_1_qn), .clk(nand_1_out), .Q(d_ff_1_q), .Qn(d_ff_1_qn), .preset(1'b0), .reset(undriven));
  nand nand_1 (nand_1_out, not_5_out, CLK);
  Pull_Resistor pull_resistor_1 (.node(pull_resistor_1_node));
  assign pull_resistor_1_node = not_6_out ? Decoded_Instruction : 44'bz;  // Controlled_Buffer controlled_buffer_1
  not not_6 (not_6_out, ExpansionControl);
  Pull_Resistor pull_resistor_2 (.node(pull_resistor_2_node));
  assign pull_resistor_2_node = ExpansionControl ? Control_Line_Expansion : 44'bz;  // Controlled_Buffer controlled_buffer_2
  assign DataOut = controlled_buffer_4_out[15] ? Instruction : 8'bz;  // Controlled_Buffer controlled_buffer_3
  or or_2 (or_2_out, controlled_buffer_4_out[14], Reset);
  and and_4 (and_4_out, not_5_out, d_ff_1_q);
  and and_5 (and_5_out, not_5_out, d_ff_1_qn);
  assign or_3_out = pull_resistor_1_node | pull_resistor_2_node;  // OR_Gate or_3, 44 bits wide
  assign {controlled_buffer_4_out[43:39], RCI, RI, RO, RUC, CRM, controlled_buffer_4_out[33], IID, DID, IDI, OUT8, controlled_buffer_4_out[28], FLOD, controlled_buffer_4_out[26], ADR, RSR, controlled_buffer_4_out[23:22], PCO, controlled_buffer_4_out[20], GRO, controlled_buffer_4_out[18], RMI, controlled_buffer_4_out[16:14], FSI, SF, CF, LF, FO, DFI, EO, EII, PSH, POP, IOI, IOO, IDO, SID} = or_1_out ? or_3_out : 44'bz;  // Controlled_Buffer controlled_buffer_4
  Pull_Resistor pull_resistor_3 (.node({controlled_buffer_4_out[43:39], RCI, RI, RO, RUC, CRM, controlled_buffer_4_out[33], IID, DID, IDI, OUT8, controlled_buffer_4_out[28], FLOD, controlled_buffer_4_out[26], ADR, RSR, controlled_buffer_4_out[23:22], PCO, controlled_buffer_4_out[20], GRO, controlled_buffer_4_out[18], RMI, controlled_buffer_4_out[16:14], FSI, SF, CF, LF, FO, DFI, EO, EII, PSH, POP, IOI, IOO, IDO, SID}));
  or or_4 (HLT, controlled_buffer_4_out[43], not_5_out);
  or or_5 (BRO, controlled_buffer_4_out[33], not_5_out);
  or or_6 (IN8, controlled_buffer_4_out[28], and_4_out);
  or or_7 (IR, controlled_buffer_4_out[26], and_5_out);
  or or_8 (MAR, controlled_buffer_4_out[23], and_5_out);
  or or_9 (PC, and_5_out, controlled_buffer_4_out[22]);
  or or_10 (GR, controlled_buffer_4_out[20], and_4_out);
  or or_11 (RMO, controlled_buffer_4_out[18], and_4_out);

  // Notes on the sheet:
  //   Decoded_Instruction: pull=down
  //   Control_Line_Expansion: pull=down
  //   IRI
  //   IRO
  //   SCR
  //   HaLT
  //   Disable Step Counter
  //   DSC
  //   Register Contoller In
  //   Register In
  //   Register Out
  //   Register Use Carry
  //   in/deCReMent
  //   Bypassed Register Out
  //   Inc address register conroller ID
  //   Dec ''
  //   address register controller ID In
  //   OUTput 8 address register bits
  //   INput 8 address register bits
  //   FulLLOaD
  //   Inc Register
  //   ADd Register
  //   ReSet Register
  //   activate MAR
  //   activate Program Counter
  //   PC Out
  //   activate General purpose address Register
  //   GaR Out
  //   RaM Out
  //   RaM In
  //   Instruction Register In
  //   IRI
  //   Instruction Register Out
  //   IRO
  //   Step Counter Reset
  //   SCR
  //   Flag Selector In
  //   Set Flags
  //   Clear Flags
  //   Load Flags
  //   Flags Out
  //   Disable Flags In
  //   alu Out
  //   alu Instruction In
  //   PuSH
  //   POP
  //   I/O In
  //   I/O Out
  //   i/o ID Out
  //   Set i/o ID
endmodule

module EEPROM_Decoder (
  input  [3:0] Step,
  input  [7:0] Instruction,
  output [47:0] DecodedInst
);

  ROM #(.addrWidth(12)) EEPROM_6 (.addr({Instruction, Step}), .data(DecodedInst[47:40]));
  ROM #(.addrWidth(12)) EEPROM_5 (.addr({Instruction, Step}), .data(DecodedInst[39:32]));
  ROM #(.addrWidth(12)) EEPROM_4 (.addr({Instruction, Step}), .data(DecodedInst[31:24]));
  ROM #(.addrWidth(12)) EEPROM_3 (.addr({Instruction, Step}), .data(DecodedInst[23:16]));
  ROM #(.addrWidth(12)) EEPROM_2 (.addr({Instruction, Step}), .data(DecodedInst[15:8]));
  ROM #(.addrWidth(12)) EEPROM_1 (.addr({Instruction, Step}), .data(DecodedInst[7:0]));

  // Notes on the sheet:
  //   contents of EEPROM_6 (hex, n*v repeats v):
  //   68*c 8 15*c 8 15*c 8 15*c 8 15*c 8 15*c 8 15*c 8 15*c 8 1871*c 8 15*c 8 15*c 8 15*c 8 15*c 8 15*c 8
  //   15*c 8 15*c 8 15*c 8 15*c 8 15*c 8 15*c 8 15*c 8 15*c 8 15*c 8 15*c 8 271*c 8 15*c 8 15*c 8 15*c 8
  //   15*c 8 15*c 8 15*c 8 15*c 8 15*c 8 15*c 8 15*c 8 15*c 8 15*c 8 15*c 8 15*c 8 15*c 8 1277*c 4 13*c
  //   contents of EEPROM_5 (hex, n*v repeats v):
  //   2 2 42 22 14*2 42 22 14*2 42 22 14*2 42 22 14*2 42 2 2 2 23 11*2 42 2 2 2 23 11*2 42 2 2 2 23 11*2
  //   42 2 2 2 23 11*2 42 2 2 2 13 11*2 42 2 2 2 13 11*2 42 2 2 2 13 11*2 42 2 2 2 13 12*2 42 20 14*2 42
  //   20 14*2 42 20 14*2 42 20 13*2 42 6 14*2 42 6 14*2 42 6 14*2 42 6 14*2 42 6 14*2 42 6 14*2 42 6 14*2
  //   42 6 14*2 42 6 14*2 42 6 14*2 42 6 14*2 42 6 14*2 42 6 14*2 42 6 14*2 42 6 14*2 42 6 14*2 42 22 14*2
  //   42 22 14*2 42 22 14*2 42 22 14*2 42 22 14*2 42 22 14*2 42 22 14*2 42 22 14*2 42 22 14*2 42 22 14*2
  //   42 22 14*2 42 22 14*2 42 22 14*2 42 22 14*2 42 22 14*2 42 22 14*2 42 22 14*2 42 22 14*2 42 22 14*2
  //   42 22 14*2 42 22 14*2 42 22 14*2 42 22 14*2 42 22 14*2 42 22 14*2 42 22 14*2 42 22 14*2 42 22 14*2
  //   42 22 14*2 42 22 14*2 42 22 14*2 42 22 15*2 42 22 14*2 42 22 14*2 42 22 14*2 42 22 14*2 42 22 14*2
  //   42 22 14*2 42 22 14*2 42 22 14*2 42 22 14*2 42 22 14*2 42 22 14*2 42 22 14*2 42 22 14*2 42 22 14*2
  //   42 22 14*2 42 22 1293*2 42 2 2 2 0 23 10*2 42 2 2 2 0 23 10*2 42 2 2 2 0 23 10*2 42 2 2 2 0 23 10*2
  //   42 2 2 2 0 23 10*2 42 2 2 2 0 23 10*2 42 2 2 2 0 23 10*2 42 2 2 2 0 23 10*2 42 2 2 2 0 23 10*2 42 2
  //   2 2 0 23 10*2 42 2 2 2 0 23 10*2 42 2 2 2 0 23 10*2 42 2 2 2 0 23 10*2 42 2 2 2 0 23 10*2 42 2 2 2 0
  //   23 10*2 42 2 2 2 0 23 1288*2
  //   contents of EEPROM_4 (hex, n*v repeats v):
  //   8 4 4 13*0 8 4 4 13*0 8 4 4 13*0 8 4 4 13*0 8 4 4 40 0 8 10*0 8 4 4 40 0 8 10*0 8 4 4 40 0 8 10*0 8
  //   4 4 40 0 8 10*0 8 4 4 40 0 8 10*0 8 4 4 40 0 8 10*0 8 4 4 40 0 8 10*0 8 4 4 40 0 8 10*0 8 4 4 13*0 8
  //   4 4 13*0 8 4 4 13*0 8 4 4 13*0 8 4 14*0 8 4 14*0 8 4 14*0 8 4 14*0 8 4 14*0 8 4 14*0 8 4 14*0 8 4
  //   14*0 8 4 14*0 8 4 14*0 8 4 14*0 8 4 14*0 8 4 14*0 8 4 14*0 8 4 14*0 8 4 14*0 8 4 14*0 8 4 14*0 8 4
  //   14*0 8 4 14*0 8 4 14*0 8 4 14*0 8 4 14*0 8 4 14*0 8 4 14*0 8 4 14*0 8 4 14*0 8 4 14*0 8 4 14*0 8 4
  //   14*0 8 4 14*0 8 4 14*0 8 4 14*0 8 4 14*0 8 4 14*0 8 4 14*0 8 4 14*0 8 4 14*0 8 4 14*0 8 4 14*0 8 4
  //   14*0 8 4 14*0 8 4 14*0 8 4 14*0 8 4 14*0 8 4 14*0 8 4 14*0 8 4 14*0 8 4 4 13*0 8 4 4 13*0 8 4 4 13*0
  //   8 4 4 13*0 8 4 4 13*0 8 4 4 13*0 8 4 4 13*0 8 4 4 13*0 8 4 4 13*0 8 4 4 13*0 8 4 4 13*0 8 4 4 13*0 8
  //   4 4 13*0 8 4 4 13*0 8 4 4 13*0 8 4 4 13*0 8 4 14*0 8 4 14*0 8 4 14*0 8 4 14*0 8 4 14*0 8 4 14*0 8 4
  //   14*0 8 4 14*0 8 4 14*0 8 4 14*0 8 4 14*0 8 4 14*0 8 4 14*0 8 4 14*0 8 4 14*0 8 4 14*0 8 4 14*0 8 4
  //   14*0 8 4 14*0 8 4 14*0 8 4 14*0 8 4 14*0 8 4 14*0 8 4 14*0 8 4 14*0 8 4 14*0 8 4 14*0 8 4 14*0 8 4
  //   14*0 8 4 14*0 8 4 14*0 8 4 14*0 8 4 14*0 8 4 14*0 8 4 14*0 8 4 14*0 8 4 14*0 8 4 14*0 8 4 14*0 8 4
  //   14*0 8 4 14*0 8 4 14*0 8 4 14*0 8 4 14*0 8 4 14*0 8 4 14*0 8 4 14*0 8 4 14*0 8 4 4 40 0 8 10*0 8 4 4
  //   40 0 8 10*0 8 4 4 40 0 8 10*0 8 4 4 40 0 8 10*0 8 4 4 40 0 8 10*0 8 4 4 40 0 8 10*0 8 4 4 40 0 8
  //   10*0 8 4 4 40 0 8 10*0 8 4 4 40 0 8 10*0 8 4 4 40 0 8 10*0 8 4 4 40 0 8 10*0 8 4 4 40 0 8 10*0 8 4 4
  //   40 0 8 10*0 8 4 4 40 0 8 10*0 8 4 4 40 0 8 10*0 8 4 4 40 0 8 10*0 8 4 14*0 8 4 14*0 8 4 14*0 8 4
  //   14*0 8 4 14*0 8 4 14*0 8 4 14*0 8 4 14*0 8 4 14*0 8 4 14*0 8 4 14*0 8 4 14*0 8 4 14*0 8 4 14*0 8 4
  //   14*0 8 4 14*0 8 4 4 40 0 8 12 9*0 8 4 4 40 0 8 12 9*0 8 4 4 40 0 8 12 9*0 8 4 4 40 0 8 12 9*0 8 4 4
  //   40 0 8 12 9*0 8 4 4 40 0 8 12 9*0 8 4 4 40 0 8 12 9*0 8 4 4 40 0 8 12 9*0 8 4 4 40 0 8 12 9*0 8 4 4
  //   40 0 8 12 9*0 8 4 4 40 0 8 12 9*0 8 4 4 40 0 8 12 9*0 8 4 4 40 0 8 12 9*0 8 4 4 40 0 8 12 9*0 8 4 4
  //   40 0 8 12 9*0 8 4 4 40 0 8 12 9*0 8 4 14*0 8 4 14*0 8 4 14*0 8 4 14*0 8 4 14*0 8 4 14*0 8 4 14*0 8 4
  //   14*0 8 4 14*0 8 4 14*0 8 4 14*0 8 4 14*0 8 4 14*0 8 4 14*0 8 4 14*0 8 4 14*0 8 4 14*0 8 4 14*0 8 4
  //   14*0 8 4 14*0 8 4 14*0 8 4 14*0 8 4 14*0 8 4 14*0 8 4 14*0 8 4 14*0 8 4 14*0 8 4 14*0 8 4 14*0 8 4
  //   14*0 8 4 14*0 8 4 14*0 8 4 14*0 8 4 14*0 8 4 14*0 8 4 14*0 8 4 14*0 8 4 14*0 8 4 14*0 8 4 14*0 8 4
  //   14*0 8 4 14*0 8 4 14*0 8 4 14*0 8 4 14*0 8 4 14*0 8 4 14*0 8 4 14*0 8 4 14*0 8 4 14*0 8 4 14*0 8 4
  //   14*0 8 4 14*0 8 4 14*0 8 4 14*0 8 4 14*0 8 4 14*0 8 4 14*0 8 4 14*0 8 4 14*0 8 4 14*0 8 4 14*0 8 4
  //   14*0 8 4 14*0 8 4 14*0 8 4 14*0 8 4 14*0 8 4 14*0 8 4 14*0 8 4 14*0 8 4 14*0 8 4 14*0 8 4 14*0 8 4
  //   14*0 8 4 14*0 8 4 14*0 8 4 14*0 8 4 14*0 8 4 14*0 8 4
  //   contents of EEPROM_3 (hex, n*v repeats v):
  //   a0 45 c0 4 12*0 a0 45 c0 4 12*0 a0 45 c0 4 12*0 a0 45 c0 4 12*0 a0 45 c0 14 0 88 14 9*0 a0 45 c0 14
  //   0 88 14 9*0 a0 45 c0 14 0 88 14 9*0 a0 45 c0 14 0 88 14 9*0 a0 45 c0 14 0 88 12 9*0 a0 45 c0 14 0 88
  //   12 9*0 a0 45 c0 14 0 88 12 9*0 a0 45 c0 14 0 88 12 9*0 a0 45 c0 4 12*0 a0 45 c0 4 12*0 a0 45 c0 4
  //   12*0 a0 45 c0 4 12*0 a0 45 14*0 a0 45 14*0 a0 45 14*0 a0 45 14*0 a0 45 14*0 a0 45 14*0 a0 45 14*0 a0
  //   45 14*0 a0 45 14*0 a0 45 14*0 a0 45 14*0 a0 45 14*0 a0 45 14*0 a0 45 14*0 a0 45 14*0 a0 45 14*0 a0
  //   45 14*0 a0 45 14*0 a0 45 14*0 a0 45 14*0 a0 45 14*0 a0 45 14*0 a0 45 14*0 a0 45 14*0 a0 45 14*0 a0
  //   45 14*0 a0 45 14*0 a0 45 14*0 a0 45 14*0 a0 45 14*0 a0 45 14*0 a0 45 14*0 a0 45 14*0 a0 45 14*0 a0
  //   45 14*0 a0 45 14*0 a0 45 14*0 a0 45 14*0 a0 45 14*0 a0 45 14*0 a0 45 14*0 a0 45 14*0 a0 45 14*0 a0
  //   45 14*0 a0 45 14*0 a0 45 14*0 a0 45 14*0 a0 45 14*0 a0 45 c0 4 12*0 a0 45 c0 4 12*0 a0 45 c0 4 12*0
  //   a0 45 c0 4 12*0 a0 45 c0 4 12*0 a0 45 c0 4 12*0 a0 45 c0 4 12*0 a0 45 c0 4 12*0 a0 45 c0 4 12*0 a0
  //   45 c0 4 12*0 a0 45 c0 4 12*0 a0 45 c0 4 12*0 a0 45 c0 4 12*0 a0 45 c0 4 12*0 a0 45 c0 4 12*0 a0 45
  //   c0 4 12*0 a0 45 14*0 a0 45 14*0 a0 45 14*0 a0 45 14*0 a0 45 14*0 a0 45 14*0 a0 45 14*0 a0 45 14*0 a0
  //   45 14*0 a0 45 14*0 a0 45 14*0 a0 45 14*0 a0 45 14*0 a0 45 14*0 a0 45 14*0 a0 45 14*0 a0 45 14*0 a0
  //   45 14*0 a0 45 14*0 a0 45 14*0 a0 45 14*0 a0 45 14*0 a0 45 14*0 a0 45 14*0 a0 45 14*0 a0 45 14*0 a0
  //   45 14*0 a0 45 14*0 a0 45 14*0 a0 45 14*0 a0 45 14*0 a0 45 14*0 a0 45 14*0 a0 45 14*0 a0 45 14*0 a0
  //   45 14*0 a0 45 14*0 a0 45 14*0 a0 45 14*0 a0 45 14*0 a0 45 14*0 a0 45 14*0 a0 45 14*0 a0 45 14*0 a0
  //   45 14*0 a0 45 14*0 a0 45 14*0 a0 45 14*0 a0 45 80 14 0 48 10*0 a0 45 80 14 0 48 10*0 a0 45 80 14 0
  //   48 10*0 a0 45 80 14 0 48 10*0 a0 45 80 14 0 48 10*0 a0 45 80 14 0 48 10*0 a0 45 80 14 0 48 10*0 a0
  //   45 80 14 0 48 10*0 a0 45 80 14 0 48 10*0 a0 45 80 14 0 48 10*0 a0 45 80 14 0 48 10*0 a0 45 80 14 0
  //   48 10*0 a0 45 80 14 0 48 10*0 a0 45 80 14 0 48 10*0 a0 45 80 14 0 48 10*0 a0 45 80 14 0 48 10*0 a0
  //   45 14*0 a0 45 14*0 a0 45 14*0 a0 45 14*0 a0 45 14*0 a0 45 14*0 a0 45 14*0 a0 45 14*0 a0 45 14*0 a0
  //   45 14*0 a0 45 14*0 a0 45 14*0 a0 45 14*0 a0 45 14*0 a0 45 14*0 a0 45 14*0 a0 45 c0 14 0 88 80 14 8*0
  //   a0 45 c0 14 0 88 80 14 8*0 a0 45 c0 14 0 88 80 14 8*0 a0 45 c0 14 0 88 80 14 8*0 a0 45 c0 14 0 88 80
  //   14 8*0 a0 45 c0 14 0 88 80 14 8*0 a0 45 c0 14 0 88 80 14 8*0 a0 45 c0 14 0 88 80 14 8*0 a0 45 c0 14
  //   0 88 80 14 8*0 a0 45 c0 14 0 88 80 14 8*0 a0 45 c0 14 0 88 80 14 8*0 a0 45 c0 14 0 88 80 14 8*0 a0
  //   45 c0 14 0 88 80 14 8*0 a0 45 c0 14 0 88 80 14 8*0 a0 45 c0 14 0 88 80 14 8*0 a0 45 c0 14 0 88 80 14
  //   8*0 a0 45 14*0 a0 45 14*0 a0 45 14*0 a0 45 14*0 a0 45 14*0 a0 45 14*0 a0 45 14*0 a0 45 14*0 a0 45
  //   14*0 a0 45 14*0 a0 45 14*0 a0 45 14*0 a0 45 14*0 a0 45 14*0 a0 45 14*0 a0 45 14*0 a0 45 14*0 a0 45
  //   14*0 a0 45 14*0 a0 45 14*0 a0 45 14*0 a0 45 14*0 a0 45 14*0 a0 45 14*0 a0 45 14*0 a0 45 14*0 a0 45
  //   14*0 a0 45 14*0 a0 45 14*0 a0 45 14*0 a0 45 14*0 a0 45 14*0 a0 45 14*0 a0 45 14*0 a0 45 14*0 a0 45
  //   14*0 a0 45 14*0 a0 45 14*0 a0 45 14*0 a0 45 14*0 a0 45 14*0 a0 45 14*0 a0 45 14*0 a0 45 14*0 a0 45
  //   14*0 a0 45 14*0 a0 45 14*0 a0 45 14*0 a0 45 14*0 a0 45 14*0 a0 45 14*0 a0 45 14*0 a0 45 14*0 a0 45
  //   14*0 a0 45 14*0 a0 45 14*0 a0 45 14*0 a0 45 14*0 a0 45 14*0 a0 45 14*0 a0 45 14*0 a0 45 14*0 a0 45
  //   14*0 a0 45 14*0 a0 45 14*0 a0 45 14*0 a0 45 14*0 a0 45 14*0 a0 45 14*0 a0 45 14*0 a0 45 14*0 a0 45
  //   14*0 a0 45 14*0 a0 45 14*0 a0 45 14*0 a0 45 14*0 a0 45 14*0 a0 45 14*0 a0 45 14*0 a0 45
  //   contents of EEPROM_2 (hex, n*v repeats v):
  //   0 0 80 0 40 13*0 80 0 40 13*0 80 0 40 13*0 80 0 40 13*0 80 4*0 40 10*0 80 4*0 40 10*0 80 4*0 40 10*0
  //   80 4*0 40 10*0 80 4*0 40 10*0 80 4*0 40 10*0 80 4*0 40 10*0 80 4*0 40 13*0 40 15*0 40 15*0 40 15*0
  //   40 12*0 80 0 40 13*0 80 0 40 13*0 80 0 40 13*0 80 0 40 13*0 80 0 40 13*0 80 0 40 13*0 80 0 40 13*0
  //   80 0 40 13*0 80 0 40 13*0 80 0 40 13*0 80 0 40 13*0 80 0 40 13*0 80 0 40 13*0 80 0 40 13*0 80 0 40
  //   13*0 80 0 40 13*0 80 0 40 13*0 80 0 40 13*0 80 0 40 13*0 80 0 40 13*0 80 0 40 13*0 80 0 40 13*0 80 0
  //   40 13*0 80 0 40 13*0 80 0 40 13*0 80 0 40 13*0 80 0 40 13*0 80 0 40 13*0 80 0 40 13*0 80 0 40 13*0
  //   80 0 40 13*0 80 0 40 13*0 80 0 40 13*0 80 0 40 13*0 80 0 40 13*0 80 0 40 13*0 80 0 40 13*0 80 0 40
  //   13*0 80 0 40 13*0 80 0 40 13*0 80 0 40 13*0 80 0 40 13*0 80 0 40 13*0 80 0 40 13*0 80 0 40 13*0 80 0
  //   40 13*0 80 0 40 13*0 80 0 40 13*0 80 0 0 40 12*0 80 0 0 40 12*0 80 0 0 40 12*0 80 0 0 40 12*0 80 0 0
  //   40 12*0 80 0 0 40 12*0 80 0 0 40 12*0 80 0 0 40 12*0 80 0 0 40 12*0 80 0 0 40 12*0 80 0 0 40 12*0 80
  //   0 0 40 12*0 80 0 0 40 12*0 80 0 0 40 12*0 80 0 0 40 12*0 80 0 0 40 784*0 40 15*0 40 15*0 40 15*0 40
  //   15*0 40 15*0 40 15*0 40 15*0 40 15*0 40 15*0 40 15*0 40 15*0 40 15*0 40 15*0 40 15*0 40 15*0 40
  //   267*0 80 5*0 40 9*0 80 5*0 40 9*0 80 5*0 40 9*0 80 5*0 40 9*0 80 5*0 40 9*0 80 5*0 40 9*0 80 5*0 40
  //   9*0 80 5*0 40 9*0 80 5*0 40 9*0 80 5*0 40 9*0 80 5*0 40 9*0 80 5*0 40 9*0 80 5*0 40 9*0 80 5*0 40
  //   9*0 80 5*0 40 9*0 80 5*0 40
  //   contents of EEPROM_1 (hex, n*v repeats v):
  //   514*0 40 80 14*0 40 80 14*0 40 80 14*0 40 80 14*0 40 80 14*0 40 80 14*0 40 80 14*0 40 80 14*0 40 80
  //   14*0 40 80 14*0 40 80 14*0 40 80 14*0 40 80 14*0 40 80 14*0 40 80 14*0 40 80 14*0 40 80 14*0 40 80
  //   14*0 40 80 14*0 40 80 14*0 40 80 14*0 40 80 14*0 40 80 14*0 40 80 14*0 40 80 14*0 40 80 14*0 40 80
  //   14*0 40 80 14*0 40 80 14*0 40 80 14*0 40 80 14*0 40 80 14*0 40 0 80 13*0 40 0 80 13*0 40 0 80 13*0
  //   40 0 80 13*0 40 0 80 13*0 40 0 80 13*0 40 0 80 13*0 40 0 80 13*0 40 0 80 13*0 40 0 80 13*0 40 0 80
  //   13*0 40 0 80 13*0 40 0 80 13*0 40 0 80 13*0 40 0 80 13*0 40 0 80
endmodule

module ManualControl (
  input  Manual_Mode,
  input  HLT,
  input  RCI,
  input  RI,
  input  RO,
  input  RUC,
  input  CRM,
  input  SFT,
  input  ROT,
  input  NOTc,
  input  BRO,
  input  IID,
  input  DID,
  input  IDI,
  input  OUT8,
  input  IN8,
  input  FLOD,
  input  IR,
  input  ADR,
  input  RSR,
  input  MAR,
  input  PC,
  input  PCO,
  input  GR,
  input  GRO,
  input  RMO,
  input  RMI,
  input  IRI,
  input  IRO,
  input  SCR,
  input  FSI,
  input  SF,
  input  CF,
  input  LF,
  input  FO,
  input  DFI,
  input  EO,
  input  EII,
  input  PSH,
  input  POP,
  input  IOI,
  input  IOO,
  input  IDO,
  input  SID,
  output Manual_Mode_Out,
  output [43:0] out_46
);

  assign out_46 = 44'hc0000000000 ^ {HLT, 1'b0, RCI, RI, RO, RUC, CRM, SFT, ROT, NOTc, BRO, IID, DID, IDI, OUT8, IN8, FLOD, IR, ADR, RSR, MAR, PC, PCO, GR, GRO, RMO, RMI, IRI, IRO, SCR, FSI, SF, CF, LF, FO, DFI, EO, EII, PSH, POP, IOI, IOO, IDO, SID};  // XOR_Gate xor_1, 44 bits wide

  assign Manual_Mode_Out = Manual_Mode;

  // Notes on the sheet:
  //   Active Low
endmodule

module HEXTo7SD (
  input  [3:0] Value,
  output [6:0] Display
);

  wire and_1_out, and_2_out, and_3_out, and_4_out, and_5_out, and_6_out, and_7_out, and_8_out, and_9_out,
       and_10_out, and_11_out, and_12_out, and_13_out, and_14_out, and_15_out, and_16_out, and_17_out,
       and_18_out, and_19_out, and_20_out, and_21_out, and_22_out, and_23_out, and_24_out, and_25_out,
       and_26_out, and_27_out, and_28_out, and_29_out, and_30_out, and_31_out, and_32_out, and_33_out,
       and_34_out, and_35_out, and_36_out, and_37_out, and_38_out, and_39_out, and_40_out, and_41_out,
       and_42_out, and_43_out, and_44_out, and_45_out, and_46_out, and_47_out, not_1_out, not_2_out,
       not_3_out, not_4_out, or_1_out, or_2_out, or_3_out, or_4_out, or_5_out, or_6_out, or_7_out, or_8_out,
       or_9_out, or_10_out, or_12_out, or_13_out, or_14_out, or_15_out, or_16_out, or_17_out, or_18_out,
       or_20_out, or_21_out, or_22_out, or_23_out;

  not not_1 (not_1_out, Value[3]);
  not not_2 (not_2_out, Value[2]);
  not not_3 (not_3_out, Value[1]);
  not not_4 (not_4_out, Value[0]);
  and and_1 (and_1_out, Value[3], not_2_out);
  and and_2 (and_2_out, not_1_out, not_3_out);
  and and_3 (and_3_out, not_1_out, not_3_out);
  and and_4 (and_4_out, not_1_out, Value[0]);
  and and_5 (and_5_out, not_1_out, not_2_out);
  and and_6 (and_6_out, not_2_out, Value[1]);
  and and_7 (and_7_out, not_2_out, not_4_out);
  and and_8 (and_8_out, Value[1], not_4_out);
  and and_9 (and_9_out, Value[3], Value[1]);
  and and_10 (and_10_out, Value[3], Value[2]);
  and and_11 (and_11_out, not_1_out, Value[2]);
  and and_12 (and_12_out, not_2_out, Value[1]);
  and and_13 (and_13_out, Value[1], not_4_out);
  and and_14 (and_14_out, not_1_out, Value[2]);
  and and_15 (and_15_out, not_2_out, not_4_out);
  and and_16 (and_16_out, not_1_out, Value[1]);
  and and_17 (and_17_out, not_1_out, Value[2]);
  and and_18 (and_18_out, Value[2], Value[1]);
  and and_19 (and_19_out, and_1_out, not_3_out);
  and and_20 (and_20_out, not_1_out, not_2_out);
  and and_21 (and_21_out, and_2_out, not_4_out);
  and and_22 (and_22_out, not_1_out, Value[1]);
  and and_23 (and_23_out, Value[3], not_3_out);
  or or_1 (or_1_out, and_3_out, and_4_out);
  and and_24 (and_24_out, not_3_out, Value[0]);
  and and_25 (and_25_out, not_1_out, Value[2]);
  and and_26 (and_26_out, Value[3], not_2_out);
  and and_27 (and_27_out, and_5_out, not_4_out);
  and and_28 (and_28_out, and_6_out, Value[0]);
  and and_29 (and_29_out, Value[2], not_3_out);
  and and_30 (and_30_out, Value[2], Value[1]);
  and and_31 (and_31_out, Value[3], not_3_out);
  or or_2 (or_2_out, and_7_out, and_8_out);
  or or_3 (or_3_out, and_9_out, and_10_out);
  and and_32 (and_32_out, not_3_out, not_4_out);
  and and_33 (and_33_out, and_11_out, not_3_out);
  or or_4 (or_4_out, and_12_out, and_13_out);
  and and_34 (and_34_out, and_14_out, not_3_out);
  and and_35 (and_35_out, Value[3], not_2_out);
  and and_36 (and_36_out, Value[3], Value[0]);
  or or_5 (or_5_out, and_15_out, and_16_out);
  and and_37 (and_37_out, and_17_out, Value[0]);
  or or_6 (or_6_out, and_18_out, and_19_out);
  and and_38 (and_38_out, Value[3], not_4_out);
  or or_7 (or_7_out, and_20_out, and_21_out);
  and and_39 (and_39_out, not_2_out, not_4_out);
  and and_40 (and_40_out, and_22_out, Value[0]);
  and and_41 (and_41_out, and_23_out, Value[0]);
  or or_8 (or_8_out, or_1_out, and_24_out);
  or or_9 (or_9_out, and_25_out, and_26_out);
  or or_10 (or_10_out, and_27_out, and_28_out);
  and and_42 (and_42_out, and_29_out, Value[0]);
  and and_43 (and_43_out, and_30_out, not_4_out);
  and and_44 (and_44_out, and_31_out, not_4_out);
  or or_11 (Display[2], or_2_out, or_3_out);
  or or_12 (or_12_out, and_32_out, and_33_out);
  and and_45 (and_45_out, Value[2], not_4_out);
  and and_46 (and_46_out, Value[3], not_2_out);
  and and_47 (and_47_out, Value[3], Value[1]);
  or or_13 (or_13_out, or_4_out, and_34_out);
  or or_14 (or_14_out, and_35_out, and_36_out);
  or or_15 (or_15_out, or_5_out, and_37_out);
  or or_16 (or_16_out, or_6_out, and_38_out);
  or or_17 (or_17_out, or_7_out, and_39_out);
  or or_18 (or_18_out, and_40_out, and_41_out);
  or or_19 (Display[4], or_8_out, or_9_out);
  or or_20 (or_20_out, or_10_out, and_42_out);
  or or_21 (or_21_out, and_43_out, and_44_out);
  or or_22 (or_22_out, or_12_out, and_45_out);
  or or_23 (or_23_out, and_46_out, and_47_out);
  or or_24 (Display[0], or_13_out, or_14_out);
  or or_25 (Display[6], or_15_out, or_16_out);
  or or_26 (Display[5], or_17_out, or_18_out);
  or or_27 (Display[3], or_20_out, or_21_out);
  or or_28 (Display[1], or_22_out, or_23_out);

  // Notes on the sheet:
  //   47 AND Gates - 11 Chips
  //   28 OR Gates - 7 Chips
  //   4 NOT Gates - 1 Chip
  //   USE BEN EATERS
  //   THIS IS BAD
  //   19
  //   15
  //   22
  //   14
  //   2
  //   38
  //   30
  //   76
  //   60
endmodule

module NOTES (
);

  wire undriven_3, undriven_4;
  wire [3:0] hct157_selctormultiplexer_1_y, hct157_selctormultiplexer_2_y;
  wire [7:0] undriven, undriven_2;

  Controlled_Buffer controlled_buffer_1 ();  // open: in, out, en
  Controlled_Inverter controlled_inverter_1 ();  // open: in, out, en
  // NOT_Gate not_1 is placed but not wired
  // AND_Gate and_1 is placed but not wired
  // OR_Gate or_1 is placed but not wired
  HCT157_SelctorMultiplexer hct157_selctormultiplexer_1 (
    .Y(hct157_selctormultiplexer_1_y), .A(undriven[3:0]), .B(undriven_2[3:0]), .S(undriven_3), .Ei(undriven_4));
  HCT157_SelctorMultiplexer hct157_selctormultiplexer_2 (
    .Y(hct157_selctormultiplexer_2_y), .A(undriven[7:4]), .B(undriven_2[7:4]), .S(undriven_3), .Ei(undriven_4));

  // Notes on the sheet:
  //   All             are 74hc245 
  //   All              are 74hct240 
  //   All             are 74hct04 
  //   All              are 74hct08 
  //   All              are 74hct32 
  //   This gotta go FAAAST
endmodule
